// Logisim project 2-1MUX-hazard.circ as structural Verilog: 2 circuits, main circuit main
module main (
  input  D0,
  input  D1,
  input  S,
  output F
);

  wire and_1_out, and_2_out, not_1_out;

  // Probe on S
  not not_1 (not_1_out, S);
  // Probe on not_1_out
  and and_1 (and_1_out, D0, not_1_out);
  cmos_or cmos_or_1 (.X(and_1_out), .Y(and_2_out), .Z(F));
  and and_2 (and_2_out, D1, S);
endmodule

module cmos_or (
  input  X,
  input  Y,
  output Z
);

  wire transistor_1_out, transistor_2_out;

  Transistor transistor_1 (.in(1'b1), .out(transistor_1_out), .gate(X));
  Transistor transistor_2 (.in(transistor_1_out), .out(transistor_2_out), .gate(Y));
  Transistor #(.\type ("n")) transistor_3 (.in(1'b0), .out(transistor_2_out), .gate(X));
  Transistor transistor_4 (.in(1'b1), .out(Z), .gate(transistor_2_out));
  Transistor #(.\type ("n")) transistor_5 (.in(1'b0), .out(transistor_2_out), .gate(Y));
  Transistor #(.\type ("n")) transistor_6 (.in(1'b0), .out(Z), .gate(transistor_2_out));

  // Notes on the sheet:
  //   Q2
  //   Q4
  //   Q1
  //   Q6
  //   Q5
  //   Q3
endmodule
