// Logisim project 3输入多数表决器.circ as structural Verilog: 5 circuits, main circuit 布尔表达� 
// Bool
module \å_�__è__达�  (
  input  X,
  input  Y,
  input  Z,
  output F
);

  wire and_1_out, and_2_out, and_3_out;

  and and_1 (and_1_out, X, Y);
  and and_2 (and_2_out, X, Z);
  and and_3 (and_3_out, Y, Z);
  or or_1 (F, and_1_out, and_2_out, and_3_out);

  // Notes on the sheet:
  //   3输入多数表决器
endmodule

// Truth
module \真�_�  (
  input  A,
  input  B,
  input  C,
  output F
);


  // Notes on the sheet:
  //   输入引脚
  //   请勿增加� 删除引脚，用隧� �标签构建电路
  //   请勿更改电路� 装外观
  //   输出引脚
  //   武汉纺织大学数字逻辑课程组
endmodule

// sTruth
module \ç__�_真�_�  (
  input  X1,
  input  X0,
  input  Y1,
  input  Y0,
  output Gt
);


  // Notes on the sheet:
  //   输入引脚
  //   请勿增加� 删除引脚，用隧� �标签构建电路
  //   请勿更改电路� 装外观
  //   输出引脚
  //   武汉纺织大学数字逻辑课程组
endmodule

// Wave
module \�_�_å_¾  (
  input  A,
  input  B,
  input  C,
  output F
);


  // Notes on the sheet:
  //   输入引脚
  //   A
  //   B
  //   C
  //   F
  //   请勿增加� 删除引脚，用隧� �标签构建电路
  //   请勿更改电路� 装外观
  //   输出引脚
  //   武汉纺织大学数字逻辑课程组
endmodule

// Kmap
module \å__è_�_¾  (
  input  A,
  input  B,
  input  C,
  input  D,
  output F
);


  // Notes on the sheet:
  //   输入引脚
  //   请勿增加� 删除引脚，用隧� �标签构建电路
  //   请勿更改电路� 装外观
  //   输出引脚
  //   武汉纺织大学数字逻辑课程组
endmodule
