// Logisim project 4-1MUX.circ as structural Verilog: 2 circuits, main circuit main
module main (
  input  D0,
  input  D1,
  input  D2,
  input  D3,
  input  S0,
  input  S1,
  output Y
);

  wire n2_1mux_1_out_4, n2_1mux_2_out_4;

  _2_1MUX u_2_1mux_1 (.in_1(D0), .in_2(D1), .in_3(S0), .out_4(n2_1mux_1_out_4));
  _2_1MUX u_2_1mux_2 (.in_1(D2), .in_2(D3), .in_3(S0), .out_4(n2_1mux_2_out_4));
  _2_1MUX u_2_1mux_3 (.in_1(n2_1mux_1_out_4), .in_2(n2_1mux_2_out_4), .in_3(S1), .out_4(Y));
endmodule

module _2_1MUX (
  input  in_1,
  input  in_2,
  input  in_3,
  output out_4
);

  wire and_1_out, and_2_out, not_1_out;

  and and_1 (and_1_out, in_1, not_1_out);
  and and_2 (and_2_out, in_2, in_3);
  not not_1 (not_1_out, in_3);
  or or_1 (out_4, and_1_out, and_2_out);

  // Other names for the same wires on the sheet: D0 = in_1; D1 = in_2; S = in_3; Y = out_4
endmodule
