// Logisim project 4^4-1MUX.circ as structural Verilog: 2 circuits, main circuit main
module main (
  input  in_1,
  input  in_2,
  input  in_3,
  input  in_4,
  input  S0,
  input  in_6,
  input  in_7,
  input  in_8,
  input  in_9,
  input  in_10,
  input  in_11,
  input  in_12,
  input  in_13,
  input  in_14,
  input  in_15,
  input  in_16,
  input  in_17,
  input  S1,
  output F0,
  output F1,
  output F2,
  output F3
);

  _4_1mux u_4_1mux_1 (.D0(in_1), .D1(in_2), .D2(in_3), .D3(in_4), .S0(S0), .S1(S1), .Y(F0));
  _4_1mux u_4_1mux_2 (.D0(in_6), .D1(in_7), .D2(in_8), .D3(in_9), .S0(S0), .S1(S1), .Y(F1));
  _4_1mux u_4_1mux_3 (.D0(in_10), .D1(in_11), .D2(in_12), .D3(in_13), .S0(S0), .S1(S1), .Y(F2));
  _4_1mux u_4_1mux_4 (.D0(in_14), .D1(in_15), .D2(in_16), .D3(in_17), .S0(S0), .S1(S1), .Y(F3));
endmodule

module _4_1mux (
  input  D0,
  input  D1,
  input  D2,
  input  D3,
  input  S0,
  input  S1,
  output Y
);

  wire n2_1mux_1_out_4, n2_1mux_2_out_4;

  _2_1MUX u_2_1mux_1 (.in_1(D0), .in_2(D1), .in_3(S0), .out_4(n2_1mux_1_out_4));
  _2_1MUX u_2_1mux_2 (.in_1(D2), .in_2(D3), .in_3(S0), .out_4(n2_1mux_2_out_4));
  _2_1MUX u_2_1mux_3 (.in_1(n2_1mux_1_out_4), .in_2(n2_1mux_2_out_4), .in_3(S1), .out_4(Y));
endmodule
