// Logisim project 奇偶校验.circ as structural Verilog: 2 circuits, main circuit main
module main (
  input  \目标W ,
  input  \目标X ,
  input  \目标Y ,
  input  \目标Z ,
  input  W,
  input  X,
  input  Y,
  input  Z,
  output out_9
);

  wire xor_1_out, xor_2_out, xor_3_out, xor_4_out;

  xor xor_1 (xor_1_out, \目标W , W);
  xor xor_2 (xor_2_out, \目标X , X);
  xor xor_3 (xor_3_out, \目标Y , Y);
  xor xor_4 (xor_4_out, \目标Z , Z);
  \奇偶检验器  \u_奇偶检验器_1  (.in_1(xor_4_out), .in_2(xor_3_out), .in_3(xor_2_out), .in_4(xor_1_out), .out_5(out_9));
endmodule

// 奇偶检验
module \奇偶检验器  (
  input  in_1,
  input  in_2,
  input  in_3,
  input  in_4,
  output out_5
);

  wire n0001_1_out_5, n0010_1_out_5, n0100_1_out_5, n0111_1_out_5, n1000_1_out_5, n1011_1_out_5,
       n1101_1_out_5, n1110_1_out_5;

  _0001 u_0001_1 (.in_1(in_1), .in_2(in_2), .in_3(in_3), .in_4(in_4), .out_5(n0001_1_out_5));
  _0010 u_0010_1 (.in_1(in_1), .in_2(in_2), .in_3(in_3), .in_4(in_4), .out_5(n0010_1_out_5));
  _0100 u_0100_1 (.in_1(in_1), .in_2(in_2), .in_3(in_3), .in_4(in_4), .out_5(n0100_1_out_5));
  _0111 u_0111_1 (.in_1(in_1), .in_2(in_2), .in_3(in_3), .in_4(in_4), .out_5(n0111_1_out_5));
  _1000 u_1000_1 (.in_1(in_1), .in_2(in_2), .in_3(in_3), .in_4(in_4), .out_5(n1000_1_out_5));
  _1011 u_1011_1 (.in_1(in_1), .in_2(in_2), .in_3(in_3), .in_4(in_4), .out_5(n1011_1_out_5));
  _1101 u_1101_1 (.in_1(in_1), .in_2(in_2), .in_3(in_3), .in_4(in_4), .out_5(n1101_1_out_5));
  _1110 u_1110_1 (.in_1(in_1), .in_2(in_2), .in_3(in_3), .in_4(in_4), .out_5(n1110_1_out_5));
  or or_1 (out_5, n0001_1_out_5, n0010_1_out_5, n0100_1_out_5, n0111_1_out_5, n1000_1_out_5, n1011_1_out_5, n1101_1_out_5, n1110_1_out_5);
endmodule
