// Logisim project 奇偶检验器.circ as structural Verilog: 9 circuits, main circuit main
module main (
  input  in_1,
  input  in_2,
  input  in_3,
  input  in_4,
  output out_5
);

  wire n0001_1_out_5, n0010_1_out_5, n0100_1_out_5, n0111_1_out_5, n1000_1_out_5, n1011_1_out_5,
       n1101_1_out_5, n1110_1_out_5;

  _0001 u_0001_1 (.in_1(in_1), .in_2(in_2), .in_3(in_3), .in_4(in_4), .out_5(n0001_1_out_5));
  _0010 u_0010_1 (.in_1(in_1), .in_2(in_2), .in_3(in_3), .in_4(in_4), .out_5(n0010_1_out_5));
  _0100 u_0100_1 (.in_1(in_1), .in_2(in_2), .in_3(in_3), .in_4(in_4), .out_5(n0100_1_out_5));
  _0111 u_0111_1 (.in_1(in_1), .in_2(in_2), .in_3(in_3), .in_4(in_4), .out_5(n0111_1_out_5));
  _1000 u_1000_1 (.in_1(in_1), .in_2(in_2), .in_3(in_3), .in_4(in_4), .out_5(n1000_1_out_5));
  _1011 u_1011_1 (.in_1(in_1), .in_2(in_2), .in_3(in_3), .in_4(in_4), .out_5(n1011_1_out_5));
  _1101 u_1101_1 (.in_1(in_1), .in_2(in_2), .in_3(in_3), .in_4(in_4), .out_5(n1101_1_out_5));
  _1110 u_1110_1 (.in_1(in_1), .in_2(in_2), .in_3(in_3), .in_4(in_4), .out_5(n1110_1_out_5));
  or or_1 (out_5, n0001_1_out_5, n0010_1_out_5, n0100_1_out_5, n0111_1_out_5, n1000_1_out_5, n1011_1_out_5, n1101_1_out_5, n1110_1_out_5);
endmodule

module _0001 (
  input  in_1,
  input  in_2,
  input  in_3,
  input  in_4,
  output out_5
);

  and and_1 (out_5, ~in_1, ~in_2, ~in_3, in_4);  // AND_Gate
endmodule

module _0010 (
  input  in_1,
  input  in_2,
  input  in_3,
  input  in_4,
  output out_5
);

  and and_1 (out_5, ~in_1, ~in_2, in_3, ~in_4);  // AND_Gate
endmodule

module _0100 (
  input  in_1,
  input  in_2,
  input  in_3,
  input  in_4,
  output out_5
);

  and and_1 (out_5, ~in_1, in_2, ~in_3, ~in_4);  // AND_Gate
endmodule

module _0111 (
  input  in_1,
  input  in_2,
  input  in_3,
  input  in_4,
  output out_5
);

  and and_1 (out_5, ~in_1, in_2, in_3, in_4);  // AND_Gate
endmodule

module _1000 (
  input  in_1,
  input  in_2,
  input  in_3,
  input  in_4,
  output out_5
);

  and and_1 (out_5, in_1, ~in_2, ~in_3, ~in_4);  // AND_Gate
endmodule

module _1011 (
  input  in_1,
  input  in_2,
  input  in_3,
  input  in_4,
  output out_5
);

  and and_1 (out_5, in_1, ~in_2, in_3, in_4);  // AND_Gate
endmodule

module _1101 (
  input  in_1,
  input  in_2,
  input  in_3,
  input  in_4,
  output out_5
);

  and and_1 (out_5, in_1, in_2, ~in_3, in_4);  // AND_Gate
endmodule

module _1110 (
  input  in_1,
  input  in_2,
  input  in_3,
  input  in_4,
  output out_5
);

  and and_1 (out_5, in_1, in_2, in_3, ~in_4);  // AND_Gate
endmodule
