// Logisim project 乘法器.circ as structural Verilog: 9 circuits, main circuit 4位无符号数乘法器
module CNTR4U (
  input  CLK,
  input  LD,
  input  CLR,
  input  D0,
  input  D1,
  input  D2,
  input  D3,
  input  ENP,
  input  ENT,
  output Q0,
  output Q1,
  output Q2,
  output Q3,
  output RCO
);

  wire and_1_out, and_2_out, and_3_out, and_4_out, and_5_out, and_6_out, and_7_out, and_8_out, and_10_out,
       and_11_out, and_12_out, and_13_out, and_14_out, and_15_out, and_16_out, and_17_out, buffer_1_out,
       d_ff_1_qn, d_ff_2_qn, d_ff_3_qn, d_ff_4_qn, not_1_out, not_2_out, not_3_out, or_1_out, or_2_out,
       or_3_out, or_4_out, xor_1_out, xor_2_out, xor_3_out, xor_4_out;

  buf buffer_1 (buffer_1_out, CLR);
  not not_1 (not_1_out, CLK);
  not not_2 (not_2_out, d_ff_1_qn);
  and and_1 (and_1_out, ~d_ff_2_qn, ~d_ff_1_qn);  // AND_Gate
  and and_2 (and_2_out, ~d_ff_3_qn, ~d_ff_2_qn, ~d_ff_1_qn);  // AND_Gate
  and and_3 (and_3_out, ENP, ENT);
  and and_4 (and_4_out, LD, ~buffer_1_out);  // AND_Gate
  and and_5 (and_5_out, not_2_out, and_3_out);
  and and_6 (and_6_out, and_1_out, and_3_out);
  and and_7 (and_7_out, and_2_out, and_3_out);
  not not_3 (not_3_out, ENT);
  and and_8 (and_8_out, ~and_4_out, ~buffer_1_out);  // AND_Gate
  xor xor_1 (xor_1_out, and_3_out, ~d_ff_1_qn);  // XOR_Gate
  xor xor_2 (xor_2_out, and_5_out, ~d_ff_2_qn);  // XOR_Gate
  xor xor_3 (xor_3_out, and_6_out, ~d_ff_3_qn);  // XOR_Gate
  xor xor_4 (xor_4_out, and_7_out, ~d_ff_4_qn);  // XOR_Gate
  and and_9 (RCO, ~d_ff_4_qn, ~d_ff_3_qn, ~d_ff_2_qn, ~d_ff_1_qn, ~not_3_out);  // AND_Gate
  and and_10 (and_10_out, and_4_out, D0);
  and and_11 (and_11_out, and_8_out, xor_1_out);
  and and_12 (and_12_out, and_4_out, D1);
  and and_13 (and_13_out, and_8_out, xor_2_out);
  and and_14 (and_14_out, and_4_out, D2);
  and and_15 (and_15_out, and_8_out, xor_3_out);
  and and_16 (and_16_out, and_4_out, D3);
  and and_17 (and_17_out, and_8_out, xor_4_out);
  or or_1 (or_1_out, and_10_out, and_11_out);
  or or_2 (or_2_out, and_12_out, and_13_out);
  or or_3 (or_3_out, and_14_out, and_15_out);
  or or_4 (or_4_out, and_16_out, and_17_out);
  D_Flip_Flop #(.trigger("falling")) d_ff_1 (
    .clk(not_1_out), .D(or_1_out), .Q(Q0), .Qn(d_ff_1_qn));  // open: preset, reset
  D_Flip_Flop #(.trigger("falling")) d_ff_2 (
    .clk(not_1_out), .D(or_2_out), .Q(Q1), .Qn(d_ff_2_qn));  // open: preset, reset
  D_Flip_Flop #(.trigger("falling")) d_ff_3 (
    .clk(not_1_out), .D(or_3_out), .Q(Q2), .Qn(d_ff_3_qn));  // open: preset, reset
  D_Flip_Flop #(.trigger("falling")) d_ff_4 (
    .clk(not_1_out), .D(or_4_out), .Q(Q3), .Qn(d_ff_4_qn));  // open: preset, reset
endmodule

module \_4位无符号数乘法器  (
  input  in_1,
  input  [3:0] X,
  input  [3:0] Y,
  output [7:0] \乘积 
);

  wire CLK, comparator_1_eq, RST, STOP;
  wire [2:0] counter_1_q;
  wire [3:0] multiplexer_1_out, multiplexer_2_out, \n4位加法器_1_s ;
  wire [3:3] \n4位加法器_1_co ;

  Clock clock_1 (.out(CLK));
  Button button_1 (.out(RST));
  Multiplexer #(.width(4), .enable("false")) multiplexer_1 (
    .in0(4'b0000), .in1(X), .out(multiplexer_1_out), .sel(\乘积 [0]));
  Hex_Digit_Display hex_digit_display_1 (.value(X));  // open: dp
  Register #(.width(4), .Select("low")) P (
    .D({\n4位加法器_1_co [3], \n4位加法器_1_s [3:1]}), .en(STOP), .Q(\乘积 [7:4]), .clk(CLK), .clr(RST));
  \_4位加法器  \u_4位加法器_1  (.S(\n4位加法器_1_s ), .CI(1'b0), .A(multiplexer_1_out), .CO(\n4位加法器_1_co [3]), .B(\乘积 [7:4]));
  Hex_Digit_Display hex_digit_display_2 (.value(Y));  // open: dp
  Register #(.width(4), .Select("low")) u_Y (.D(multiplexer_2_out), .en(STOP), .Q(\乘积 [3:0]), .clk(CLK), .clr(RST));
  Multiplexer #(.width(4), .enable("false")) multiplexer_2 (
    .in0({\n4位加法器_1_s [0], \乘积 [3:1]}), .in1(Y), .out(multiplexer_2_out), .sel(in_1));
  Hex_Digit_Display hex_digit_display_3 (.value(\乘积 [7:4]));  // open: dp
  Hex_Digit_Display hex_digit_display_4 (.value(\乘积 [3:0]));  // open: dp
  Counter #(.width(3), .max('h5), .ongoal("stay")) counter_1 (
    .Q(counter_1_q), .clk(CLK), .clr(RST));  // open: load, D, count, carry, preset, down
  Comparator #(.width(3)) comparator_1 (.a(counter_1_q), .b(3'b101), .eq(comparator_1_eq));  // open: gt, lt
  not not_1 (STOP, comparator_1_eq);
  // Probe on X
  // Probe on Y
  // Probe on \乘积 

  // Other names for the same wires on the sheet: LOAD = in_1; Z[7:0] = \乘积 

  // Notes on the sheet:
  //   输入引脚区
  //   X
  //   4位无符号数一位乘法器
  //   =
  //   输出引脚区
  //   ×
  //   =
endmodule

module \_8位移位器  (
  input  [7:0] in_1,
  input  L_R,
  input  [2:0] in_3,
  input  AL,
  output [7:0] out_5
);

  wire [0:0] not_1_out;
  wire [7:0] multiplexer_2_out, multiplexer_3_out;
  wire [7:7] multiplexer_1_out;

  Multiplexer #(.enable("false")) multiplexer_1 (.in0(1'b1), .in1(1'b0), .out(multiplexer_1_out[7]), .sel(AL));
  not not_1 (not_1_out[0], L_R);
  Multiplexer #(.select(2), .width(8), .enable("false")) multiplexer_2 (
    .in0(in_1), .in1(in_1), .in2({in_1[6:0], 1'b0}), .in3({multiplexer_1_out[7], in_1[7:1]}),
    .out(multiplexer_2_out), .sel({in_3[0], not_1_out[0]}));
  Multiplexer #(.select(2), .width(8), .enable("false")) multiplexer_3 (
    .in0(multiplexer_2_out), .in1(multiplexer_2_out), .in2({multiplexer_2_out[5:0], 2'b00}),
    .in3({{2{multiplexer_1_out[7]}}, multiplexer_2_out[7:2]}), .out(multiplexer_3_out),
    .sel({in_3[1], not_1_out[0]}));
  Multiplexer #(.select(2), .width(8), .enable("false")) multiplexer_4 (
    .in0(multiplexer_3_out), .in1(multiplexer_3_out), .in2({multiplexer_3_out[3:0], 4'b0000}),
    .in3({{4{multiplexer_1_out[7]}}, multiplexer_3_out[7:4]}), .out(out_5), .sel({in_3[2], not_1_out[0]}));
endmodule

module \_4位加法器  (
  input  CI,
  input  [3:0] A,
  input  [3:0] B,
  output [3:0] S,
  output CO
);

  wire fa_1_co, fa_2_co, fa_3_co;

  FA fa_1 (.A(A[0]), .B(B[0]), .CI(CI), .S(S[0]), .CO(fa_1_co));
  FA fa_2 (.A(A[1]), .B(B[1]), .CI(fa_1_co), .S(S[1]), .CO(fa_2_co));
  FA fa_3 (.A(A[2]), .B(B[2]), .CI(fa_2_co), .S(S[2]), .CO(fa_3_co));
  FA fa_4 (.A(A[3]), .B(B[3]), .CI(fa_3_co), .S(S[3]), .CO(CO));
endmodule

module \全加器  (
  input  CI,
  input  A,
  input  B,
  output S,
  output CO
);

  wire and_1_out, and_2_out, and_3_out, xor_2_out;

  or or_1 (CO, and_2_out, and_3_out, and_1_out);
  and and_1 (and_1_out, A, B);
  and and_2 (and_2_out, B, CI);
  and and_3 (and_3_out, A, CI);
  xor xor_1 (S, CI, xor_2_out);
  xor xor_2 (xor_2_out, A, B);
endmodule

module \_4位寄存器  (
  input  CLK,
  input  CLR,
  input  LIN,
  input  D,
  input  C,
  input  B,
  input  A,
  input  RIN,
  input  S1,
  input  S0,
  output QD,
  output QC,
  output QB,
  output QA
);

  wire _00_2_out, _00_3_out, _00_4_out, _00_5_out, _00_out, _01_2_out, _01_3_out, _01_4_out, _01_out,
       _10_2_out, _10_3_out, _10_4_out, _10_out, _11_2_out, _11_3_out, _11_out, not_1_out, not_2_out,
       not_3_out, not_4_out, not_5_out, not_6_out, or_1_out, or_2_out, or_3_out, or_4_out;

  not not_1 (not_1_out, CLK);
  not not_2 (not_2_out, CLR);
  not not_3 (not_3_out, S1);
  not not_4 (not_4_out, S0);
  not not_5 (not_5_out, not_3_out);
  not not_6 (not_6_out, not_4_out);
  and _10 (_10_out, not_2_out, LIN, not_5_out, not_4_out);
  and _00 (_00_out, not_2_out, QD, not_3_out, not_4_out);
  and _11 (_11_out, not_2_out, D, not_5_out, not_6_out);
  and _01 (_01_out, not_2_out, QC, not_6_out, not_3_out);
  and _10_2 (_10_2_out, not_2_out, QD, not_5_out, not_4_out);
  and _00_2 (_00_2_out, not_2_out, QC, not_3_out, not_4_out);
  and _11_2 (_11_2_out, not_2_out, C, not_5_out, not_6_out);
  and _01_2 (_01_2_out, not_2_out, QB, not_3_out, not_6_out);
  and _10_3 (_10_3_out, not_2_out, QC, not_5_out, not_4_out);
  and _00_3 (_00_3_out, not_2_out, QB, not_3_out, not_4_out);
  and _00_4 (_00_4_out, not_2_out, B, not_5_out, not_6_out);
  and _01_3 (_01_3_out, not_2_out, QA, not_3_out, not_6_out);
  and _10_4 (_10_4_out, not_2_out, QB, not_5_out, not_4_out);
  and _00_5 (_00_5_out, not_2_out, QA, not_3_out, not_4_out);
  and _11_3 (_11_3_out, not_2_out, A, not_6_out, not_5_out);
  and _01_4 (_01_4_out, not_2_out, RIN, not_3_out, not_6_out);
  or or_1 (or_1_out, _10_out, _00_out, _11_out, _01_out);
  or or_2 (or_2_out, _10_2_out, _00_2_out, _11_2_out, _01_2_out);
  or or_3 (or_3_out, _10_3_out, _00_3_out, _00_4_out, _01_3_out);
  or or_4 (or_4_out, _10_4_out, _00_5_out, _11_3_out, _01_4_out);
  D_Flip_Flop #(.trigger("falling")) u_QD (.clk(not_1_out), .D(or_1_out), .Q(QD));  // open: Qn, preset, reset
  D_Flip_Flop #(.trigger("falling")) u_QC (.clk(not_1_out), .D(or_2_out), .Q(QC));  // open: Qn, preset, reset
  D_Flip_Flop #(.trigger("falling")) u_QB (.clk(not_1_out), .D(or_3_out), .Q(QB));  // open: Qn, preset, reset
  D_Flip_Flop #(.trigger("falling")) u_QA (.clk(not_1_out), .D(or_4_out), .Q(QA));  // open: Qn, preset, reset
endmodule

module _123 (
);

  wire CLK, LOAD, \n4位加法器_1_co , not_1_out, not_2_out, RST;
  wire [1:0] multiplexer_1_out;
  wire [3:0] multiplexer_2_out, multiplexer_3_out, \n4位加法器_1_s , X, Y;
  wire [7:0] Z;

  Multiplexer #(.width(2), .enable("false")) multiplexer_1 (
    .in0(2'b01), .in1(2'b11), .out(multiplexer_1_out), .sel(LOAD));
  not not_1 (not_1_out, LOAD);
  Multiplexer #(.width(4), .enable("false")) multiplexer_2 (
    .in0(4'b0000), .in1(\n4位加法器_1_s ), .out(multiplexer_2_out), .sel(not_1_out));
  \_4位寄存器  \u_4位寄存器_1  (
    .CLK(CLK), .CLR(RST), .LIN(Z[4]), .D(Y[3]), .C(Y[2]), .B(Y[1]), .A(Y[0]), .S1(multiplexer_1_out[0]),
    .S0(multiplexer_1_out[1]), .QD(Z[3]), .QC(Z[2]), .QB(Z[1]), .QA(Z[0]));  // open: RIN
  not not_2 (not_2_out, multiplexer_1_out[1]);
  Multiplexer #(.width(4), .enable("false")) multiplexer_3 (
    .in0(4'b0000), .in1(X), .out(multiplexer_3_out), .sel(Z[0]));
  \_4位寄存器  \u_4位寄存器_2  (
    .CLK(CLK), .CLR(RST), .LIN(\n4位加法器_1_co ), .D(multiplexer_2_out[3]), .C(multiplexer_2_out[2]),
    .B(multiplexer_2_out[1]), .A(multiplexer_2_out[0]), .S1(multiplexer_1_out[0]), .S0(not_2_out), .QD(Z[4]),
    .QC(Z[5]), .QB(Z[6]), .QA(Z[7]));  // open: RIN
  \_4位加法器  \u_4位加法器_1  (
    .S(\n4位加法器_1_s ), .CI(1'b0), .A(multiplexer_3_out), .CO(\n4位加法器_1_co ), .B({Z[4], Z[5], Z[6], Z[7]}));
  Hex_Digit_Display hex_digit_display_1 (.value(\n4位加法器_1_s ));  // open: dp
endmodule

module \布斯乘法器  (
  input  in_1,
  input  [3:0] X,
  input  [3:0] Y,
  output [7:0] \乘积 
);

  wire CLK, comparator_1_eq, RST, STOP;
  wire [0:0] register_1_q;
  wire [2:0] counter_1_q;
  wire [3:0] multiplexer_1_out, multiplexer_2_out, \n4位加法器_1_s , \相反数_1_out_2 ;

  Clock clock_1 (.out(CLK));
  \相反数  \u_相反数_1  (.in_1(X), .out_2(\相反数_1_out_2 ));
  Multiplexer #(.select(2), .width(4), .enable("false")) multiplexer_1 (
    .in0(4'b0000), .in1(X), .in2(\相反数_1_out_2 ), .in3(4'b0000), .out(multiplexer_1_out),
    .sel({\乘积 [0], register_1_q[0]}));
  Register #(.width(1), .Select("low")) register_1 (
    .D(\乘积 [0]), .Q(register_1_q[0]), .clk(CLK), .clr(RST));  // open: en
  Register #(.width(4), .Select("low")) P (
    .D({{2{\n4位加法器_1_s [3]}}, \n4位加法器_1_s [2:1]}), .en(STOP), .Q(\乘积 [7:4]), .clk(CLK), .clr(RST));
  \_4位加法器  \u_4位加法器_1  (.S(\n4位加法器_1_s ), .CI(1'b0), .A(multiplexer_1_out), .B(\乘积 [7:4]));  // open: CO
  Button button_1 (.out(RST));
  Register #(.width(4), .Select("low")) u_Y (.D(multiplexer_2_out), .en(STOP), .Q(\乘积 [3:0]), .clk(CLK), .clr(RST));
  Multiplexer #(.width(4), .enable("false")) multiplexer_2 (
    .in0({\n4位加法器_1_s [0], \乘积 [3:1]}), .in1(Y), .out(multiplexer_2_out), .sel(in_1));
  Counter #(.width(3), .max('h5), .ongoal("stay")) counter_1 (
    .Q(counter_1_q), .clk(CLK), .clr(RST));  // open: load, D, count, carry, preset, down
  Comparator #(.width(3)) comparator_1 (.a(counter_1_q), .b(3'b101), .eq(comparator_1_eq));  // open: gt, lt
  not not_1 (STOP, comparator_1_eq);

  // Other names for the same wires on the sheet: LOAD = in_1; Z[7:0] = \乘积 

  // Notes on the sheet:
  //   输入引脚区
  //   辅助位
endmodule

module \相反数  (
  input  [3:0] in_1,
  output [3:0] out_2
);

  wire [3:0] xor_1_out;

  xor xor_1 (xor_1_out[0], 1'b1, in_1[0]);
  xor xor_2 (xor_1_out[1], 1'b1, in_1[1]);
  xor xor_3 (xor_1_out[2], 1'b1, in_1[2]);
  xor xor_4 (xor_1_out[3], 1'b1, in_1[3]);
  \_4位加法器  \u_4位加法器_1  (.S(out_2), .CI(1'b0), .A(xor_1_out), .B(4'b0001));  // open: CO
endmodule
