// Logisim project 寄存器堆实验.circ as structural Verilog: 2 circuits, main circuit 寄存器堆读写
module regfiles (
  input  [4:0] R1_num,
  input  [31:0] Din,
  input  [4:0] R2_num,
  input  [4:0] Write_Reg_num,
  input  Write_Enable,
  input  Clock,
  output [31:0] Reg1Out,
  output [31:0] Reg2Out
);

  wire and_1_out, and_2_out, and_3_out, and_4_out, and_5_out, and_6_out, and_7_out, and_8_out, and_9_out,
       and_10_out, and_11_out, and_12_out, and_13_out, and_14_out, and_15_out, and_16_out, and_17_out,
       and_18_out, and_19_out, and_20_out, and_21_out, and_22_out, and_23_out, and_24_out, and_25_out,
       and_26_out, and_27_out, and_28_out, and_29_out, and_30_out, and_31_out, and_32_out, and_33_out,
       and_34_out, and_35_out, and_36_out, decoder_1_out0, decoder_1_out1, decoder_1_out2, decoder_1_out3,
       decoder_2_out0, decoder_2_out1, decoder_2_out2, decoder_2_out3, decoder_2_out4, decoder_2_out5,
       decoder_2_out6, decoder_2_out7, decoder_3_out0, decoder_3_out1, decoder_3_out2, decoder_3_out3,
       decoder_3_out4, decoder_3_out5, decoder_3_out6, decoder_3_out7, decoder_4_out0, decoder_4_out1,
       decoder_4_out2, decoder_4_out3, decoder_4_out4, decoder_4_out5, decoder_4_out6, decoder_4_out7,
       decoder_5_out0, decoder_5_out1, decoder_5_out2, decoder_5_out3, decoder_5_out4, decoder_5_out5,
       decoder_5_out7;
  wire [31:0] register_1_q, register_2_q, register_3_q, register_4_q, register_5_q, register_6_q,
       register_7_q, register_8_q, register_9_q, register_10_q, register_11_q, register_12_q, register_13_q,
       register_14_q, register_15_q, register_16_q, register_17_q, register_18_q, register_19_q,
       register_20_q, register_21_q, register_22_q, register_23_q, register_24_q, register_25_q,
       register_26_q, register_27_q, register_28_q, register_29_q, register_30_q, register_31_q,
       register_32_q;

  Decoder #(.select(2), .enable("false")) decoder_1 (
    .out0(decoder_1_out0), .out1(decoder_1_out1), .out2(decoder_1_out2), .out3(decoder_1_out3),
    .sel(Write_Reg_num[4:3]));
  Decoder #(.select(3), .enable("false")) decoder_2 (
    .out0(decoder_2_out0), .out1(decoder_2_out1), .out2(decoder_2_out2), .out3(decoder_2_out3),
    .out4(decoder_2_out4), .out5(decoder_2_out5), .out6(decoder_2_out6), .out7(decoder_2_out7),
    .sel(Write_Reg_num[2:0]));
  Decoder #(.select(3), .enable("false")) decoder_3 (
    .out0(decoder_3_out0), .out1(decoder_3_out1), .out2(decoder_3_out2), .out3(decoder_3_out3),
    .out4(decoder_3_out4), .out5(decoder_3_out5), .out6(decoder_3_out6), .out7(decoder_3_out7),
    .sel(Write_Reg_num[2:0]));
  Decoder #(.select(3), .enable("false")) decoder_4 (
    .out0(decoder_4_out0), .out1(decoder_4_out1), .out2(decoder_4_out2), .out3(decoder_4_out3),
    .out4(decoder_4_out4), .out5(decoder_4_out5), .out6(decoder_4_out6), .out7(decoder_4_out7),
    .sel(Write_Reg_num[2:0]));
  Decoder #(.select(3), .enable("false")) decoder_5 (
    .out0(decoder_5_out0), .out1(decoder_5_out1), .out2(decoder_5_out2), .out3(decoder_5_out3),
    .out4(decoder_5_out4), .out5(decoder_5_out5), .out6(decoder_5_out5), .out7(decoder_5_out7),
    .sel(Write_Reg_num[2:0]));
  and and_1 (and_1_out, Write_Enable, decoder_1_out0);
  and and_2 (and_2_out, decoder_1_out1, Write_Enable);
  and and_3 (and_3_out, decoder_1_out2, Write_Enable);
  and and_4 (and_4_out, decoder_1_out3, Write_Enable);
  and and_5 (and_5_out, decoder_2_out0, and_1_out);
  and and_6 (and_6_out, decoder_2_out1, and_1_out);
  and and_7 (and_7_out, decoder_2_out2, and_1_out);
  and and_8 (and_8_out, decoder_2_out3, and_1_out);
  and and_9 (and_9_out, decoder_2_out4, and_1_out);
  and and_10 (and_10_out, decoder_2_out5, and_1_out);
  and and_11 (and_11_out, decoder_2_out6, and_1_out);
  and and_12 (and_12_out, decoder_2_out7, and_1_out);
  and and_13 (and_13_out, decoder_3_out0, and_2_out);
  and and_14 (and_14_out, decoder_3_out1, and_2_out);
  and and_15 (and_15_out, decoder_3_out2, and_2_out);
  and and_16 (and_16_out, decoder_3_out3, and_2_out);
  and and_17 (and_17_out, decoder_3_out4, and_2_out);
  and and_18 (and_18_out, decoder_3_out5, and_2_out);
  and and_19 (and_19_out, decoder_3_out6, and_2_out);
  and and_20 (and_20_out, decoder_3_out7, and_2_out);
  and and_21 (and_21_out, decoder_4_out0, and_3_out);
  and and_22 (and_22_out, decoder_4_out1, and_3_out);
  and and_23 (and_23_out, decoder_4_out2, and_3_out);
  and and_24 (and_24_out, decoder_4_out3, and_3_out);
  and and_25 (and_25_out, decoder_4_out4, and_3_out);
  and and_26 (and_26_out, decoder_4_out5, and_3_out);
  and and_27 (and_27_out, decoder_4_out6, and_3_out);
  and and_28 (and_28_out, decoder_4_out7, and_3_out);
  and and_29 (and_29_out, decoder_5_out0, and_4_out);
  and and_30 (and_30_out, decoder_5_out1, and_4_out);
  and and_31 (and_31_out, decoder_5_out2, and_4_out);
  and and_32 (and_32_out, decoder_5_out3, and_4_out);
  and and_33 (and_33_out, decoder_5_out4, and_4_out);
  and and_34 (and_34_out, decoder_5_out5, and_4_out);
  and and_35 (and_35_out, decoder_5_out5, and_4_out);
  and and_36 (and_36_out, decoder_5_out7, and_4_out);
  Register #(.width(32), .Select("low")) register_1 (
    .D(Din), .en(and_5_out), .Q(register_1_q), .clk(Clock));  // open: clr
  Register #(.width(32), .Select("low")) register_2 (
    .D(Din), .en(and_6_out), .Q(register_2_q), .clk(Clock));  // open: clr
  Register #(.width(32), .Select("low")) register_3 (
    .D(Din), .en(and_7_out), .Q(register_3_q), .clk(Clock));  // open: clr
  Register #(.width(32), .Select("low")) register_4 (
    .D(Din), .en(and_8_out), .Q(register_4_q), .clk(Clock));  // open: clr
  Register #(.width(32), .Select("low")) register_5 (.D(Din), .en(and_9_out), .Q(register_5_q));  // open: clk, clr
  Register #(.width(32), .Select("low")) register_6 (
    .D(Din), .en(and_10_out), .Q(register_6_q), .clk(Clock));  // open: clr
  Register #(.width(32), .Select("low")) register_7 (
    .D(Din), .en(and_11_out), .Q(register_7_q), .clk(Clock));  // open: clr
  Register #(.width(32), .Select("low")) register_8 (
    .D(Din), .en(and_12_out), .Q(register_8_q), .clk(Clock));  // open: clr
  Register #(.width(32), .Select("low")) register_9 (
    .D(Din), .en(and_13_out), .Q(register_9_q), .clk(Clock));  // open: clr
  Register #(.width(32), .Select("low")) register_10 (
    .D(Din), .en(and_14_out), .Q(register_10_q), .clk(Clock));  // open: clr
  Register #(.width(32), .Select("low")) register_11 (
    .D(Din), .en(and_15_out), .Q(register_11_q), .clk(Clock));  // open: clr
  Register #(.width(32), .Select("low")) register_12 (
    .D(Din), .en(and_16_out), .Q(register_12_q), .clk(Clock));  // open: clr
  Register #(.width(32), .Select("low")) register_13 (
    .D(Din), .en(and_17_out), .Q(register_13_q), .clk(Clock));  // open: clr
  Register #(.width(32), .Select("low")) register_14 (
    .D(Din), .en(and_18_out), .Q(register_14_q), .clk(Clock));  // open: clr
  Register #(.width(32), .Select("low")) register_15 (
    .D(Din), .en(and_19_out), .Q(register_15_q), .clk(Clock));  // open: clr
  Register #(.width(32), .Select("low")) register_16 (
    .D(Din), .en(and_20_out), .Q(register_16_q), .clk(Clock));  // open: clr
  Register #(.width(32), .Select("low")) register_17 (
    .D(Din), .en(and_21_out), .Q(register_17_q), .clk(Clock));  // open: clr
  Register #(.width(32), .Select("low")) register_18 (
    .D(Din), .en(and_22_out), .Q(register_18_q), .clk(Clock));  // open: clr
  Register #(.width(32), .Select("low")) register_19 (
    .D(Din), .en(and_23_out), .Q(register_19_q), .clk(Clock));  // open: clr
  Register #(.width(32), .Select("low")) register_20 (
    .D(Din), .en(and_24_out), .Q(register_20_q), .clk(Clock));  // open: clr
  Register #(.width(32), .Select("low")) register_21 (
    .D(Din), .en(and_25_out), .Q(register_21_q), .clk(Clock));  // open: clr
  Register #(.width(32), .Select("low")) register_22 (
    .D(Din), .en(and_26_out), .Q(register_22_q), .clk(Clock));  // open: clr
  Register #(.width(32), .Select("low")) register_23 (
    .D(Din), .en(and_27_out), .Q(register_23_q), .clk(Clock));  // open: clr
  Register #(.width(32), .Select("low")) register_24 (
    .D(Din), .en(and_28_out), .Q(register_24_q), .clk(Clock));  // open: clr
  Register #(.width(32), .Select("low")) register_25 (
    .D(Din), .en(and_29_out), .Q(register_25_q), .clk(Clock));  // open: clr
  Register #(.width(32), .Select("low")) register_26 (
    .D(Din), .en(and_30_out), .Q(register_26_q), .clk(Clock));  // open: clr
  Register #(.width(32), .Select("low")) register_27 (
    .D(Din), .en(and_31_out), .Q(register_27_q), .clk(Clock));  // open: clr
  Register #(.width(32), .Select("low")) register_28 (
    .D(Din), .en(and_32_out), .Q(register_28_q), .clk(Clock));  // open: clr
  Register #(.width(32), .Select("low")) register_29 (
    .D(Din), .en(and_33_out), .Q(register_29_q), .clk(Clock));  // open: clr
  Register #(.width(32), .Select("low")) register_30 (
    .D(Din), .en(and_34_out), .Q(register_30_q), .clk(Clock));  // open: clr
  Register #(.width(32), .Select("low")) register_31 (
    .D(Din), .en(and_35_out), .Q(register_31_q), .clk(Clock));  // open: clr
  Register #(.width(32), .Select("low")) register_32 (
    .D(Din), .en(and_36_out), .Q(register_32_q), .clk(Clock));  // open: clr
  Multiplexer #(.select(5), .width(32), .enable("false")) multiplexer_1 (
    .in0(register_1_q), .in1(register_2_q), .in2(register_3_q), .in3(register_4_q), .in4(register_5_q),
    .in5(register_6_q), .in6(register_7_q), .in7(register_8_q), .in8(register_9_q), .in9(register_10_q),
    .in10(register_11_q), .in11(register_12_q), .in12(register_13_q), .in13(register_14_q),
    .in14(register_15_q), .in15(register_16_q), .in16(register_17_q), .in17(register_18_q),
    .in18(register_19_q), .in19(register_20_q), .in20(register_21_q), .in21(register_22_q),
    .in22(register_23_q), .in23(register_24_q), .in24(register_25_q), .in25(register_26_q),
    .in26(register_27_q), .in27(register_28_q), .in28(register_29_q), .in29(register_30_q),
    .in30(register_31_q), .in31(register_32_q), .out(Reg1Out), .sel(R1_num));
  Multiplexer #(.select(5), .width(32), .enable("false")) multiplexer_2 (
    .in0(register_1_q), .in1(register_2_q), .in2(register_3_q), .in3(register_4_q), .in4(register_5_q),
    .in5(register_6_q), .in6(register_7_q), .in7(register_8_q), .in8(register_9_q), .in9(register_10_q),
    .in10(register_11_q), .in11(register_12_q), .in12(register_13_q), .in13(register_14_q),
    .in14(register_15_q), .in15(register_16_q), .in16(register_17_q), .in17(register_18_q),
    .in18(register_19_q), .in19(register_20_q), .in20(register_21_q), .in21(register_22_q),
    .in22(register_23_q), .in23(register_24_q), .in24(register_25_q), .in25(register_26_q),
    .in26(register_27_q), .in27(register_28_q), .in28(register_29_q), .in29(register_30_q),
    .in30(register_31_q), .in31(register_32_q), .out(Reg2Out), .sel(R2_num));

  // Other names for the same wires on the sheet: CLK = Clock; RA[4:0] = R1_num; RB[4:0] = R2_num; RDA[31:0] = Reg1Out;
  //   RDB[31:0] = Reg2Out; RW[4:0] = Write_Reg_num; WE = Write_Enable
endmodule

module \寄存器堆读写  (
  input  [4:0] R1_num,
  input  [4:0] R2_num,
  input  [4:0] Write_Reg_num,
  input  [31:0] Din,
  input  Write_Enable,
  output [31:0] Reg1out,
  output [31:0] Reg2out
);

  wire CLK_out;

  Clock CLK (.out(CLK_out));
  regfiles regfiles_1 (
    .R1_num(R1_num), .Din(Din), .R2_num(R2_num), .Write_Reg_num(Write_Reg_num), .Write_Enable(Write_Enable),
    .Clock(CLK_out), .Reg1Out(Reg1out), .Reg2Out(Reg2out));
endmodule
