// Logisim project 移位寄存器实验.circ as structural Verilog: 2 circuits, main circuit main
module main (
  input  CLR,
  input  S1,
  input  S0
);

  wire CLK_out, xor_1_out;
  wire [3:0] shrg4u_1_qd;

  Clock CLK (.out(CLK_out));
  SHRG4U shrg4u_1 (
    .CLK(CLK_out), .CLR(CLR), .LIN(xor_1_out), .D(1'b0), .C(1'b0), .B(1'b0), .A(1'b1), .S1(S1), .S0(S0),
    .QD(shrg4u_1_qd[0]), .QC(shrg4u_1_qd[1]), .QB(shrg4u_1_qd[2]), .QA(shrg4u_1_qd[3]));  // open: RIN
  xor xor_1 (xor_1_out, shrg4u_1_qd[2], shrg4u_1_qd[3]);
  Hex_Digit_Display hex_digit_display_1 (.value(shrg4u_1_qd));  // open: dp
  // Digital_Oscilloscope #(.nState(20), .frontlines("falling")) digital_oscilloscope_1: pin names not known; wires that end beside it: CLK_out, shrg4u_1_qd[0], shrg4u_1_qd[1], shrg4u_1_qd[2], shrg4u_1_qd[3]
endmodule

module SHRG4U (
  input  CLK,
  input  CLR,
  input  LIN,
  input  D,
  input  C,
  input  B,
  input  A,
  input  RIN,
  input  S1,
  input  S0,
  output QD,
  output QC,
  output QB,
  output QA
);

  wire _00_2_out, _00_3_out, _00_4_out, _00_5_out, _00_out, _01_2_out, _01_3_out, _01_4_out, _01_out,
       _10_2_out, _10_3_out, _10_4_out, _10_out, _11_2_out, _11_3_out, _11_out, not_1_out, not_2_out,
       not_3_out, not_4_out, not_5_out, not_6_out, or_1_out, or_2_out, or_3_out, or_4_out;

  not not_1 (not_1_out, CLK);
  not not_2 (not_2_out, CLR);
  not not_3 (not_3_out, S1);
  not not_4 (not_4_out, S0);
  not not_5 (not_5_out, not_3_out);
  not not_6 (not_6_out, not_4_out);
  and _10 (_10_out, not_2_out, LIN, not_5_out, not_4_out);
  and _00 (_00_out, not_2_out, QD, not_3_out, not_4_out);
  and _11 (_11_out, not_2_out, D, not_5_out, not_6_out);
  and _01 (_01_out, not_2_out, QC, not_6_out, not_3_out);
  and _10_2 (_10_2_out, not_2_out, QD, not_5_out, not_4_out);
  and _00_2 (_00_2_out, not_2_out, QC, not_3_out, not_4_out);
  and _11_2 (_11_2_out, not_2_out, C, not_5_out, not_6_out);
  and _01_2 (_01_2_out, not_2_out, QB, not_3_out, not_6_out);
  and _10_3 (_10_3_out, not_2_out, QC, not_5_out, not_4_out);
  and _00_3 (_00_3_out, not_2_out, QB, not_3_out, not_4_out);
  and _00_4 (_00_4_out, not_2_out, B, not_5_out, not_6_out);
  and _01_3 (_01_3_out, not_2_out, QA, not_3_out, not_6_out);
  and _10_4 (_10_4_out, not_2_out, QB, not_5_out, not_4_out);
  and _00_5 (_00_5_out, not_2_out, QA, not_3_out, not_4_out);
  and _11_3 (_11_3_out, not_2_out, A, not_6_out, not_5_out);
  and _01_4 (_01_4_out, not_2_out, RIN, not_3_out, not_6_out);
  or or_1 (or_1_out, _10_out, _00_out, _11_out, _01_out);
  or or_2 (or_2_out, _10_2_out, _00_2_out, _11_2_out, _01_2_out);
  or or_3 (or_3_out, _10_3_out, _00_3_out, _00_4_out, _01_3_out);
  or or_4 (or_4_out, _10_4_out, _00_5_out, _11_3_out, _01_4_out);
  D_Flip_Flop #(.trigger("falling")) u_QD (.clk(not_1_out), .D(or_1_out), .Q(QD));  // open: Qn, preset, reset
  D_Flip_Flop #(.trigger("falling")) u_QC (.clk(not_1_out), .D(or_2_out), .Q(QC));  // open: Qn, preset, reset
  D_Flip_Flop #(.trigger("falling")) u_QB (.clk(not_1_out), .D(or_3_out), .Q(QB));  // open: Qn, preset, reset
  D_Flip_Flop #(.trigger("falling")) u_QA (.clk(not_1_out), .D(or_4_out), .Q(QA));  // open: Qn, preset, reset
endmodule
