// Logisim project 计数器&数字时钟实验.circ as structural Verilog: 4 circuits, main circuit CNTR4U
module CNTR4U (
  input  CLK,
  input  LD,
  input  CLR,
  input  D0,
  input  D1,
  input  D2,
  input  D3,
  input  ENP,
  input  ENT,
  output Q0,
  output Q1,
  output Q2,
  output Q3,
  output RCO
);

  wire and_1_out, and_2_out, and_3_out, and_4_out, and_5_out, and_6_out, and_7_out, and_8_out, and_10_out,
       and_11_out, and_12_out, and_13_out, and_14_out, and_15_out, and_16_out, and_17_out, buffer_1_out,
       d_ff_1_qn, d_ff_2_qn, d_ff_3_qn, d_ff_4_qn, not_1_out, not_2_out, not_3_out, or_1_out, or_2_out,
       or_3_out, or_4_out, xor_1_out, xor_2_out, xor_3_out, xor_4_out;

  buf buffer_1 (buffer_1_out, CLR);
  not not_1 (not_1_out, CLK);
  not not_2 (not_2_out, d_ff_1_qn);
  and and_1 (and_1_out, ~d_ff_2_qn, ~d_ff_1_qn);  // AND_Gate
  and and_2 (and_2_out, ~d_ff_3_qn, ~d_ff_2_qn, ~d_ff_1_qn);  // AND_Gate
  and and_3 (and_3_out, ENP, ENT);
  and and_4 (and_4_out, LD, ~buffer_1_out);  // AND_Gate
  and and_5 (and_5_out, not_2_out, and_3_out);
  and and_6 (and_6_out, and_1_out, and_3_out);
  and and_7 (and_7_out, and_2_out, and_3_out);
  not not_3 (not_3_out, ENT);
  and and_8 (and_8_out, ~and_4_out, ~buffer_1_out);  // AND_Gate
  xor xor_1 (xor_1_out, and_3_out, ~d_ff_1_qn);  // XOR_Gate
  xor xor_2 (xor_2_out, and_5_out, ~d_ff_2_qn);  // XOR_Gate
  xor xor_3 (xor_3_out, and_6_out, ~d_ff_3_qn);  // XOR_Gate
  xor xor_4 (xor_4_out, and_7_out, ~d_ff_4_qn);  // XOR_Gate
  and and_9 (RCO, ~d_ff_4_qn, ~d_ff_3_qn, ~d_ff_2_qn, ~d_ff_1_qn, ~not_3_out);  // AND_Gate
  and and_10 (and_10_out, and_4_out, D0);
  and and_11 (and_11_out, and_8_out, xor_1_out);
  and and_12 (and_12_out, and_4_out, D1);
  and and_13 (and_13_out, and_8_out, xor_2_out);
  and and_14 (and_14_out, and_4_out, D2);
  and and_15 (and_15_out, and_8_out, xor_3_out);
  and and_16 (and_16_out, and_4_out, D3);
  and and_17 (and_17_out, and_8_out, xor_4_out);
  or or_1 (or_1_out, and_10_out, and_11_out);
  or or_2 (or_2_out, and_12_out, and_13_out);
  or or_3 (or_3_out, and_14_out, and_15_out);
  or or_4 (or_4_out, and_16_out, and_17_out);
  D_Flip_Flop #(.trigger("falling")) d_ff_1 (
    .clk(not_1_out), .D(or_1_out), .Q(Q0), .Qn(d_ff_1_qn));  // open: preset, reset
  D_Flip_Flop #(.trigger("falling")) d_ff_2 (
    .clk(not_1_out), .D(or_2_out), .Q(Q1), .Qn(d_ff_2_qn));  // open: preset, reset
  D_Flip_Flop #(.trigger("falling")) d_ff_3 (
    .clk(not_1_out), .D(or_3_out), .Q(Q2), .Qn(d_ff_3_qn));  // open: preset, reset
  D_Flip_Flop #(.trigger("falling")) d_ff_4 (
    .clk(not_1_out), .D(or_4_out), .Q(Q3), .Qn(d_ff_4_qn));  // open: preset, reset
endmodule

module \十进制计数器  (
  input  LD,
  input  EN
);

  wire and_1_out, CLK_out, cntr4u_1_rco;
  wire [3:0] cntr4u_1_q0;

  Clock CLK (.out(CLK_out));
  CNTR4U cntr4u_1 (
    .LD(LD), .CLR(and_1_out), .D0(1'b1), .D1(1'b1), .D2(1'b0), .D3(1'b0), .ENP(EN), .ENT(EN),
    .Q0(cntr4u_1_q0[0]), .Q1(cntr4u_1_q0[1]), .Q2(cntr4u_1_q0[2]), .Q3(cntr4u_1_q0[3]), .RCO(cntr4u_1_rco),
    .CLK(CLK_out));
  and and_1 (and_1_out, cntr4u_1_q0[0], ~cntr4u_1_q0[1], ~cntr4u_1_q0[2], cntr4u_1_q0[3]);  // AND_Gate
  Hex_Digit_Display hex_digit_display_1 (.value(cntr4u_1_q0));  // open: dp
  LED led_1 (.in(cntr4u_1_rco));
endmodule

module \数字时钟_存疑  (
  input  \设定闹钟 ,
  input  \闹钟开关 ,
  input  \设置初值 ,
  input  [3:0] \时高位 ,
  input  [3:0] \时低位 ,
  input  [3:0] \分高位 ,
  input  [3:0] \分低位 ,
  input  [3:0] \秒高位 ,
  input  [3:0] \秒低位 
);

  wire and_3_out, and_4_out, and_5_out, and_6_out, and_7_out, and_8_out, and_9_out, and_10_out, and_11_out,
       and_12_out, and_13_out, and_14_out, and_15_out, and_16_out, and_17_out, and_18_out, and_19_out,
       and_20_out, and_21_out, and_22_out, CLK, d_ff_1_q, d_ff_2_q, LED, multiplexer_1_out,
       multiplexer_2_out, multiplexer_3_out, multiplexer_4_out, multiplexer_5_out, not_1_out, or_1_out, STOP,
       \蜂鸣使能 , \闹钟使能 ;
  wire [3:0] H0, H1, M0, M1, S0, S1;

  Clock \u_时钟  (.out(CLK));
  Button \u_关闭闹钟  (.out(STOP));
  and and_1 (LED, and_9_out, and_12_out, and_15_out, and_18_out);
  and and_2 (\蜂鸣使能 , and_9_out, and_12_out, and_15_out, and_18_out, and_21_out, and_22_out);
  and and_3 (and_3_out, and_8_out, and_11_out, and_14_out, and_17_out);
  and and_4 (and_4_out, and_3_out, and_5_out);
  D_Flip_Flop #(.trigger("falling")) d_ff_1 (.clk(CLK), .D(and_4_out), .Q(d_ff_1_q));  // open: Qn, preset, reset
  and and_5 (and_5_out, and_6_out, H1[1]);
  D_Flip_Flop #(.trigger("falling")) d_ff_2 (.clk(CLK), .D(and_4_out), .Q(d_ff_2_q));  // open: Qn, preset, reset
  or or_1 (or_1_out, d_ff_1_q, and_20_out);
  and and_6 (and_6_out, H0[0], H0[1]);
  Hex_Digit_Display hex_digit_display_1 (.value(H1));  // open: dp
  Hex_Digit_Display hex_digit_display_2 (.value(H0), .dp(1'b1));
  and and_7 (and_7_out, ~\设置初值 , and_8_out);  // AND_Gate
  and and_8 (and_8_out, S0[0], S0[3]);
  and and_9 (and_9_out, ~S0[0], ~S0[1], ~S0[2], ~S0[3]);  // AND_Gate
  Multiplexer #(.enable("false")) multiplexer_1 (.in0(and_9_out), .in1(CLK), .out(multiplexer_1_out), .sel(\设置初值 ));
  and and_10 (and_10_out, ~\设置初值 , and_11_out);  // AND_Gate
  and and_11 (and_11_out, S1[0], S1[2]);
  and and_12 (and_12_out, ~S1[0], ~S1[1], ~S1[2], ~S1[3]);  // AND_Gate
  Multiplexer #(.enable("false")) multiplexer_2 (.in0(and_12_out), .in1(CLK), .out(multiplexer_2_out), .sel(\设置初值 ));
  and and_13 (and_13_out, ~\设置初值 , and_14_out);  // AND_Gate
  and and_14 (and_14_out, M0[0], M0[3]);
  and and_15 (and_15_out, ~M0[0], ~M0[1], ~M0[2], ~M0[3]);  // AND_Gate
  Multiplexer #(.enable("false")) multiplexer_3 (.in0(and_15_out), .in1(CLK), .out(multiplexer_3_out), .sel(\设置初值 ));
  and and_16 (and_16_out, ~\设置初值 , and_17_out);  // AND_Gate
  and and_17 (and_17_out, M1[0], M1[2]);
  and and_18 (and_18_out, ~M1[0], ~M1[1], ~M1[2], ~M1[3]);  // AND_Gate
  Multiplexer #(.enable("false")) multiplexer_4 (.in0(and_18_out), .in1(CLK), .out(multiplexer_4_out), .sel(\设置初值 ));
  and and_19 (and_19_out, ~\设置初值 , or_1_out);  // AND_Gate
  and and_20 (and_20_out, H0[0], H0[3]);
  and and_21 (and_21_out, ~H0[0], ~H0[1], ~H0[2], ~H0[3]);  // AND_Gate
  Multiplexer #(.enable("false")) multiplexer_5 (.in0(and_21_out), .in1(CLK), .out(multiplexer_5_out), .sel(\设置初值 ));
  and and_22 (and_22_out, ~H1[0], ~H1[1], ~H1[2], ~H1[3]);  // AND_Gate
  Hex_Digit_Display hex_digit_display_3 (.value(M1));  // open: dp
  Hex_Digit_Display hex_digit_display_4 (.value(M0), .dp(1'b1));
  CNTR4U cntr4u_1 (
    .LD(\设置初值 ), .CLR(and_7_out), .D0(\秒低位 [0]), .D1(\秒低位 [1]), .D2(\秒低位 [2]), .D3(\秒低位 [3]), .ENP(1'b1),
    .ENT(1'b1), .Q0(S0[0]), .Q1(S0[1]), .Q2(S0[2]), .Q3(S0[3]), .CLK(CLK));  // open: RCO
  CNTR4U cntr4u_2 (
    .LD(\设置初值 ), .CLR(and_10_out), .D0(\秒高位 [0]), .D1(\秒高位 [1]), .D2(\秒高位 [2]), .D3(\秒高位 [3]), .ENP(1'b1),
    .ENT(1'b1), .Q0(S1[0]), .Q1(S1[1]), .Q2(S1[2]), .Q3(S1[3]), .CLK(multiplexer_1_out));  // open: RCO
  CNTR4U cntr4u_3 (
    .LD(\设置初值 ), .CLR(and_13_out), .D0(\分低位 [0]), .D1(\分低位 [1]), .D2(\分低位 [2]), .D3(\分低位 [3]), .ENP(1'b1),
    .ENT(1'b1), .Q0(M0[0]), .Q1(M0[1]), .Q2(M0[2]), .Q3(M0[3]), .CLK(multiplexer_2_out));  // open: RCO
  CNTR4U cntr4u_4 (
    .LD(\设置初值 ), .CLR(and_16_out), .D0(\分高位 [0]), .D1(\分高位 [1]), .D2(\分高位 [2]), .D3(\分高位 [3]), .ENP(1'b1),
    .ENT(1'b1), .Q0(M1[0]), .Q1(M1[1]), .Q2(M1[2]), .Q3(M1[3]), .CLK(multiplexer_3_out));  // open: RCO
  CNTR4U cntr4u_5 (
    .LD(\设置初值 ), .CLR(and_19_out), .D0(\时低位 [0]), .D1(\时低位 [1]), .D2(\时低位 [2]), .D3(\时低位 [3]), .ENP(1'b1),
    .ENT(1'b1), .Q0(H0[0]), .Q1(H0[1]), .Q2(H0[2]), .Q3(H0[3]), .CLK(multiplexer_4_out));  // open: RCO
  CNTR4U cntr4u_6 (
    .LD(\设置初值 ), .CLR(d_ff_2_q), .D0(\时高位 [0]), .D1(\时高位 [1]), .D2(\时高位 [2]), .D3(\时高位 [3]), .ENP(1'b1),
    .ENT(1'b1), .Q0(H1[0]), .Q1(H1[1]), .Q2(H1[2]), .Q3(H1[3]), .CLK(multiplexer_5_out));  // open: RCO
  Hex_Digit_Display hex_digit_display_5 (.value(S1));  // open: dp
  Hex_Digit_Display hex_digit_display_6 (.value(S0), .dp(1'b1));
  LED \u_整点点亮  (.in(LED));
  // Buzzer buzzer_1: pin names not known; wires that end beside it: 14'h1000, \蜂鸣使能 , 7'b0110000
  not not_1 (not_1_out, \设定闹钟 );
  // Buzzer buzzer_2: pin names not known; wires that end beside it: 14'h1, \闹钟使能 , 7'b1010000
  \闹钟模块  \u_闹钟模块_1  (
    .in_1(\时高位 ), .in_2(\时低位 ), .in_3(\分高位 ), .in_4(\分低位 ), .in_5(\秒高位 ), .in_7(\秒低位 ), .in_13(M1),
    .in_12(H0), .in_16(S0), .in_15(S1), .in_14(M0), .out_17(\闹钟使能 ), .SET(not_1_out), .CLK(CLK), .in_11(H1),
    .EN(\闹钟开关 ), .STOP(STOP));

  // Other names for the same wires on the sheet: CLOCK = \闹钟开关 ; LD = \设置初值 ; SET = \设定闹钟 

  // Notes on the sheet:
  //   初始时间
  //   BCD码
  //   输入信号
  //   数字时钟
  //   频率
  //   蜂鸣器
  //   音量
  //   频率
  //   蜂鸣器
  //   音量
endmodule

module \闹钟模块  (
  input  [3:0] in_1,
  input  [3:0] in_2,
  input  [3:0] in_3,
  input  [3:0] in_4,
  input  [3:0] in_5,
  input  STOP,
  input  [3:0] in_7,
  input  SET,
  input  CLK,
  input  EN,
  input  [3:0] in_11,
  input  [3:0] in_12,
  input  [3:0] in_13,
  input  [3:0] in_14,
  input  [3:0] in_15,
  input  [3:0] in_16,
  output out_17
);

  wire comparator_1_eq, multiplexer_1_out;
  wire [23:0] register_1_q;

  Register #(.width(24), .Select("low")) register_1 (
    .D({in_7, in_5, in_4, in_3, in_2, in_1}), .en(SET), .Q(register_1_q), .clk(CLK));  // open: clr
  Comparator #(.width(24), .mode("unsigned")) comparator_1 (
    .a(register_1_q), .b({in_16, in_15, in_14, in_13, in_12, in_11}), .eq(comparator_1_eq));  // open: gt, lt
  Multiplexer #(.enable("false")) multiplexer_1 (.in0(1'b0), .in1(comparator_1_eq), .out(multiplexer_1_out), .sel(EN));
  Counter #(.width(1), .max('h1), .ongoal("stay")) counter_1 (
    .Q(out_17), .clk(multiplexer_1_out), .clr(STOP));  // open: load, D, count, carry, preset, down
endmodule
