// Logisim project 3-8译码器.circ as structural Verilog: 1 circuit, main circuit main
module main (
  input  G1,
  input  G2A_L,
  input  G2B_L,
  input  A,
  input  B,
  input  C,
  output Y0_L,
  output Y0_L_2,
  output Y0_L_3,
  output Y0_L_4,
  output Y0_L_5,
  output Y0_L_6,
  output Y0_L_7,
  output Y0_L_8
);

  wire and_1_out, not_1_out, not_2_out, not_3_out, not_4_out, not_5_out, not_6_out, not_7_out;

  not not_1 (not_1_out, G1);
  and and_1 (and_1_out, ~not_1_out, ~G2A_L, ~G2B_L);  // AND_Gate
  not not_2 (not_2_out, A);
  not not_3 (not_3_out, B);
  not not_4 (not_4_out, C);
  not not_5 (not_5_out, not_2_out);
  not not_6 (not_6_out, not_3_out);
  not not_7 (not_7_out, not_4_out);
  nand nand_1 (Y0_L, and_1_out, not_2_out, not_3_out, not_4_out);
  nand nand_2 (Y0_L_2, and_1_out, not_3_out, not_4_out, not_5_out);
  nand nand_3 (Y0_L_3, and_1_out, not_2_out, not_4_out, not_6_out);
  nand nand_4 (Y0_L_4, and_1_out, not_4_out, not_5_out, not_6_out);
  nand nand_5 (Y0_L_5, and_1_out, not_2_out, not_3_out, not_7_out);
  nand nand_6 (Y0_L_6, and_1_out, not_3_out, not_5_out, not_7_out);
  nand nand_7 (Y0_L_7, and_1_out, not_2_out, not_6_out, not_7_out);
  nand nand_8 (Y0_L_8, and_1_out, not_6_out, not_5_out, not_7_out);
endmodule
