// Logisim project 32位桶形移位器.circ as structural Verilog: 1 circuit, main circuit main
module main (
  input  [31:0] in_1,
  input  [5:0] in_2,
  input  L_R,
  input  AL,
  output [31:0] out_5
);

  wire [0:0] not_1_out;
  wire [31:0] multiplexer_2_out, multiplexer_3_out, multiplexer_4_out, multiplexer_5_out, multiplexer_6_out;
  wire [31:31] multiplexer_1_out;

  not not_1 (not_1_out[0], L_R);
  Multiplexer #(.enable("false")) multiplexer_1 (.in0(1'b0), .in1(in_1[31]), .out(multiplexer_1_out[31]), .sel(AL));
  Multiplexer #(.select(2), .width(32), .enable("false")) multiplexer_2 (
    .in0(in_1), .in1(in_1), .in2({in_1[30:0], 1'b0}), .in3({multiplexer_1_out[31], in_1[31:1]}),
    .out(multiplexer_2_out), .sel({in_2[0], not_1_out[0]}));
  Multiplexer #(.select(2), .width(32), .enable("false")) multiplexer_3 (
    .in0(multiplexer_2_out), .in1(multiplexer_2_out), .in2({multiplexer_2_out[29:0], 2'b00}),
    .in3({{2{multiplexer_1_out[31]}}, multiplexer_2_out[31:2]}), .out(multiplexer_3_out),
    .sel({in_2[1], not_1_out[0]}));
  Multiplexer #(.select(2), .width(32), .enable("false")) multiplexer_4 (
    .in0(multiplexer_3_out), .in1(multiplexer_3_out), .in2({multiplexer_3_out[27:0], 4'b0000}),
    .in3({{4{multiplexer_1_out[31]}}, multiplexer_3_out[31:4]}), .out(multiplexer_4_out),
    .sel({in_2[2], not_1_out[0]}));
  Multiplexer #(.select(2), .width(32), .enable("false")) multiplexer_5 (
    .in0(multiplexer_4_out), .in1(multiplexer_4_out), .in2({multiplexer_4_out[27:0], 4'b0000}),
    .in3({{4{multiplexer_1_out[31]}}, multiplexer_4_out[31:4]}), .out(multiplexer_5_out),
    .sel({in_2[3], not_1_out[0]}));
  Multiplexer #(.select(2), .width(32), .enable("false")) multiplexer_6 (
    .in0(multiplexer_5_out), .in1(multiplexer_5_out), .in2({multiplexer_5_out[23:0], {8{1'b0}}}),
    .in3({{8{multiplexer_1_out[31]}}, multiplexer_5_out[31:8]}), .out(multiplexer_6_out),
    .sel({in_2[4], not_1_out[0]}));
  Multiplexer #(.select(2), .width(32), .enable("false")) multiplexer_7 (
    .in0(multiplexer_6_out), .in1(multiplexer_6_out), .in2({multiplexer_6_out[15:0], {16{1'b0}}}),
    .in3({{16{multiplexer_1_out[31]}}, multiplexer_6_out[31:16]}), .out(out_5), .sel({in_2[5], not_1_out[0]}));
endmodule
