// Logisim project 8位桶形移位器.circ as structural Verilog: 1 circuit, main circuit main
module main (
  input  [7:0] in_1,
  input  L_R,
  input  [2:0] in_3,
  input  AL,
  output [7:0] out_5
);

  wire [0:0] not_1_out;
  wire [7:0] multiplexer_2_out, multiplexer_3_out;
  wire [7:7] multiplexer_1_out;

  not not_1 (not_1_out[0], L_R);
  Multiplexer #(.enable("false")) multiplexer_1 (.in0(in_1[7]), .in1(1'b0), .out(multiplexer_1_out[7]), .sel(AL));
  Multiplexer #(.select(2), .width(8), .enable("false")) multiplexer_2 (
    .in0(in_1), .in1(in_1), .in2({in_1[6:0], 1'b0}), .in3({multiplexer_1_out[7], in_1[7:1]}),
    .out(multiplexer_2_out), .sel({in_3[0], not_1_out[0]}));
  Multiplexer #(.select(2), .width(8), .enable("false")) multiplexer_3 (
    .in0(multiplexer_2_out), .in1(multiplexer_2_out), .in2({multiplexer_2_out[5:0], 2'b00}),
    .in3({{2{multiplexer_1_out[7]}}, multiplexer_2_out[7:2]}), .out(multiplexer_3_out),
    .sel({in_3[1], not_1_out[0]}));
  Multiplexer #(.select(2), .width(8), .enable("false")) multiplexer_4 (
    .in0(multiplexer_3_out), .in1(multiplexer_3_out), .in2({multiplexer_3_out[3:0], 4'b0000}),
    .in3({{4{multiplexer_1_out[7]}}, multiplexer_3_out[7:4]}), .out(out_5), .sel({in_3[2], not_1_out[0]}));
endmodule
