// Logisim project ALU.circ as structural Verilog: 3 circuits, main circuit main
module main (
  input  A,
  input  B,
  input  [2:0] SELECT,
  output F
);

  wire adder_1_out, and_1_out, not_1_out, not_2_out, or_1_out, subtractor_1_out, xnor_1_out;

  Adder #(.width(1)) adder_1 (.a(A), .b(B), .out(adder_1_out));  // open: cin, cout
  Subtractor #(.width(1)) subtractor_1 (.a(A), .b(B), .out(subtractor_1_out));  // open: bin, bout
  and and_1 (and_1_out, A, B);
  or or_1 (or_1_out, A, B);
  xnor xnor_1 (xnor_1_out, A, B);
  not not_1 (not_1_out, A);
  not not_2 (not_2_out, B);
  Multiplexer #(.select(3), .enable("false")) multiplexer_1 (
    .in0(adder_1_out), .in1(subtractor_1_out), .in2(and_1_out), .in3(or_1_out), .in4(xnor_1_out),
    .in5(not_1_out), .in6(A), .in7(not_2_out), .out(F), .sel(SELECT));
endmodule

module ALU (
  input  [3:0] A,
  input  [3:0] B,
  input  [2:0] SELECT,
  output OF,
  output CF,
  output CF_2,
  output [3:0] F,
  output SF,
  output ZF
);

  wire subtractor_1_bout, xor_1_out, xor_2_out;
  wire [3:0] adder_1_out, and_1_out, not_1_out, not_2_out, or_1_out, subtractor_1_out, xnor_1_out;

  xor xor_1 (xor_1_out, A[3], B[3]);
  Adder #(.width(4)) adder_1 (.a(A), .b(B), .out(adder_1_out), .cout(CF));  // open: cin
  Subtractor #(.width(4)) subtractor_1 (.a(A), .b(B), .out(subtractor_1_out), .bout(subtractor_1_bout));  // open: bin
  assign and_1_out = A & B;  // AND_Gate and_1, 4 bits wide
  assign or_1_out = A | B;  // OR_Gate or_1, 4 bits wide
  assign xnor_1_out = ~(A ^ B);  // XNOR_Gate xnor_1, 4 bits wide
  assign not_1_out = ~A;  // NOT_Gate not_1, 4 bits wide
  assign not_2_out = ~B;  // NOT_Gate not_2, 4 bits wide
  Multiplexer #(.select(3), .width(4), .enable("false")) multiplexer_1 (
    .in0(adder_1_out), .in1(subtractor_1_out), .in2(and_1_out), .in3(or_1_out), .in4(xnor_1_out),
    .in5(not_1_out), .in6(A), .in7(not_2_out), .out(F), .sel(SELECT));
  nor nor_1 (ZF, F[3], F[2], F[1], F[0]);
  xor xor_2 (xor_2_out, xor_1_out, F[3]);
  xor xor_3 (OF, xor_2_out, CF);
  not not_3 (CF_2, subtractor_1_bout);

  assign SF = F[3];
endmodule

module _4_ALU (
  input  [3:0] A,
  input  [3:0] B,
  input  [2:0] SELECT,
  output [3:0] F
);

  wire [3:0] adder_1_out, and_1_out, not_1_out, not_2_out, or_1_out, subtractor_1_out, xnor_1_out;

  Adder #(.width(4)) adder_1 (.a(A), .b(B), .out(adder_1_out));  // open: cin, cout
  Subtractor #(.width(4)) subtractor_1 (.a(A), .b(B), .out(subtractor_1_out));  // open: bin, bout
  assign and_1_out = A & B;  // AND_Gate and_1, 4 bits wide
  assign or_1_out = A | B;  // OR_Gate or_1, 4 bits wide
  assign xnor_1_out = ~(A ^ B);  // XNOR_Gate xnor_1, 4 bits wide
  assign not_1_out = ~A;  // NOT_Gate not_1, 4 bits wide
  assign not_2_out = ~B;  // NOT_Gate not_2, 4 bits wide
  Multiplexer #(.select(3), .width(4), .enable("false")) multiplexer_1 (
    .in0(adder_1_out), .in1(subtractor_1_out), .in2(and_1_out), .in3(or_1_out), .in4(xnor_1_out),
    .in5(not_1_out), .in6(A), .in7(not_2_out), .out(F), .sel(SELECT));
endmodule
