// Logisim project “南大”.circ as structural Verilog: 1 circuit, main circuit main
module main (
);

  DotMatrix #(.matrixcols(16), .matrixrows(16)) dotmatrix_1 (
    .col0({16{1'b0}}), .col1({16{1'b0}}), .col2(16'h3fc), .col3(16'h200), .col4(16'h1208), .col5(16'h12a8),
    .col6(16'h1268), .col7(16'h7e3c), .col8(16'h1268), .col9(16'h12a8), .col10(16'h1208), .col11(16'h200),
    .col12(16'h204), .col13(16'h3fc), .col14({16{1'b0}}), .col15({16{1'b0}}));
  DotMatrix #(.matrixcols(16), .matrixrows(16)) dotmatrix_2 (
    .col0({16{1'b0}}), .col1(16'h2), .col2(16'h4), .col3(16'h208), .col4(16'h210), .col5(16'h220),
    .col6(16'h240), .col7(16'h7f80), .col8(16'h7f80), .col9(16'h240), .col10(16'h220), .col11(16'h210),
    .col12(16'h208), .col13(16'h4), .col14(16'h2), .col15({16{1'b0}}));
endmodule
