// Logisim project 全加器FA.circ as structural Verilog: 3 circuits, main circuit 4FA
module FA (
  input  CI,
  input  A,
  input  B,
  output S,
  output CO
);

  wire and_1_out, and_2_out, and_3_out, xor_2_out;

  or or_1 (CO, and_3_out, and_2_out, and_1_out);
  and and_1 (and_1_out, A, B);
  and and_2 (and_2_out, A, CI);
  and and_3 (and_3_out, B, CI);
  xor xor_1 (S, CI, xor_2_out);
  xor xor_2 (xor_2_out, A, B);
endmodule

module _4FA (
  input  CI,
  input  [3:0] A,
  input  [3:0] B,
  output [3:0] S,
  output CO
);

  wire fa_1_co, fa_2_co, fa_3_co;

  FA fa_1 (.A(A[0]), .B(B[0]), .CI(CI), .S(S[0]), .CO(fa_1_co));
  FA fa_2 (.A(A[1]), .B(B[1]), .CI(fa_1_co), .S(S[1]), .CO(fa_2_co));
  FA fa_3 (.A(A[2]), .B(B[2]), .CI(fa_2_co), .S(S[2]), .CO(fa_3_co));
  FA fa_4 (.A(A[3]), .B(B[3]), .CI(fa_3_co), .S(S[3]), .CO(CO));
endmodule

module _4FA_2 (
  input  CI,
  input  [3:0] A,
  input  [3:0] B,
  output [3:0] S,
  output ZF,
  output CF,
  output CO,
  output OF,
  output SF
);

  wire fa_1_co, fa_2_co, fa_4_co, xor_1_out, xor_2_out;

  FA fa_1 (.A(A[0]), .B(B[0]), .CI(CI), .S(S[0]), .CO(fa_1_co));
  xor xor_1 (xor_1_out, A[3], B[3]);
  xor xor_2 (xor_2_out, xor_1_out, CO);
  xor xor_3 (OF, xor_2_out, S[3]);
  FA fa_2 (.A(A[1]), .B(B[1]), .CI(fa_1_co), .S(S[1]), .CO(fa_2_co));
  FA fa_3 (.A(A[3]), .B(B[3]), .CI(fa_4_co), .S(S[3]), .CO(CO));
  FA fa_4 (.A(A[2]), .B(B[2]), .CI(fa_2_co), .S(S[2]), .CO(fa_4_co));
  NotExactlyOne xnor_1 (.out(ZF), .in0(S[3]), .in1(S[2]), .in2(S[1]), .in3(S[0]));
  xor xor_4 (CF, CO, CI);

  assign SF = S[3];
endmodule
