// Logisim project 汉明码.circ as structural Verilog
module \_7ä½_æ__æ_Žç__æ__éªŒç_µè  (
  input  [6:0] A,
  output [6:0] Y,
  output NO_ERROR
);

  wire \n3_8è_ç_å_1_y0_l , \n3_8è_ç_å_1_y0_l_2 , \n3_8è_ç_å_1_y0_l_3 , \n3_8è_ç_å_1_y0_l_4 ,
       \n3_8è_ç_å_1_y0_l_5 , \n3_8è_ç_å_1_y0_l_6 , \n3_8è_ç_å_1_y0_l_7 , \n3_8è_ç_å_1_y0_l_8 ,
       \n4ä½_å_æ_éªœç_µè_1_out_5 , \n4ä½_å_æ_éªœç_µè_2_out_5 , \n4ä½_å_æ_éªœç_µè_3_out_5 , not_1_out,
       not_2_out, not_3_out, not_4_out, not_5_out, not_6_out, not_7_out;

  \_4ä½_å__æ__éªŒç_µè  \u_4ä½_å_æ_éªœç_µè_1  (
    .in_1(A[6]), .in_2(A[4]), .in_3(A[2]), .in_4(A[0]), .out_5(\n4ä½_å_æ_éªœç_µè_1_out_5 ));
  \_4ä½_å__æ__éªŒç_µè  \u_4ä½_å_æ_éªœç_µè_2  (
    .in_1(A[6]), .in_2(A[5]), .in_3(A[2]), .in_4(A[1]), .out_5(\n4ä½_å_æ_éªœç_µè_2_out_5 ));
  \_4ä½_å__æ__éªŒç_µè  \u_4ä½_å_æ_éªœç_µè_3  (
    .in_1(A[6]), .in_2(A[5]), .in_3(A[4]), .in_4(A[3]), .out_5(\n4ä½_å_æ_éªœç_µè_3_out_5 ));
  \_3_8è__ç__å  \u_3_8è_ç_å_1  (
    .Y0_L(\n3_8è_ç_å_1_y0_l ), .Y0_L_2(\n3_8è_ç_å_1_y0_l_2 ), .G1(1'b1), .Y0_L_3(\n3_8è_ç_å_1_y0_l_3 ),
    .G2A_L(1'b0), .G2B_L(1'b0), .Y0_L_4(\n3_8è_ç_å_1_y0_l_4 ), .Y0_L_5(\n3_8è_ç_å_1_y0_l_5 ),
    .Y0_L_6(\n3_8è_ç_å_1_y0_l_6 ), .A(\n4ä½_å_æ_éªœç_µè_1_out_5 ), .Y0_L_7(\n3_8è_ç_å_1_y0_l_7 ),
    .B(\n4ä½_å_æ_éªœç_µè_2_out_5 ), .Y0_L_8(\n3_8è_ç_å_1_y0_l_8 ), .C(\n4ä½_å_æ_éªœç_µè_3_out_5 ));
  xor xor_1 (Y[0], A[0], not_1_out);
  not not_1 (not_1_out, \n3_8è_ç_å_1_y0_l_2 );
  xor xor_2 (Y[1], A[1], not_2_out);
  not not_2 (not_2_out, \n3_8è_ç_å_1_y0_l_3 );
  xor xor_3 (Y[2], A[2], not_3_out);
  not not_3 (not_3_out, \n3_8è_ç_å_1_y0_l_4 );
  xor xor_4 (Y[3], A[3], not_4_out);
  not not_4 (not_4_out, \n3_8è_ç_å_1_y0_l_5 );
  xor xor_5 (Y[4], A[4], not_5_out);
  not not_5 (not_5_out, \n3_8è_ç_å_1_y0_l_6 );
  xor xor_6 (Y[5], A[5], not_6_out);
  not not_6 (not_6_out, \n3_8è_ç_å_1_y0_l_7 );
  xor xor_7 (Y[6], A[6], not_7_out);
  not not_7 (not_7_out, \n3_8è_ç_å_1_y0_l_8 );
  LED ERROR (.in(\n3_8è_ç_å_1_y0_l ));
  not not_8 (NO_ERROR, \n3_8è_ç_å_1_y0_l );
endmodule

module \_3_8è__ç__å  (
  input  G1,
  input  G2A_L,
  input  G2B_L,
  input  A,
  input  B,
  input  C,
  output Y0_L,
  output Y0_L_2,
  output Y0_L_3,
  output Y0_L_4,
  output Y0_L_5,
  output Y0_L_6,
  output Y0_L_7,
  output Y0_L_8
);

  wire and_1_out, not_1_out, not_2_out, not_3_out, not_4_out, not_5_out, not_6_out, not_7_out;

  not not_1 (not_1_out, G1);
  not not_2 (not_2_out, A);
  not not_3 (not_3_out, B);
  not not_4 (not_4_out, C);
  and and_1 (and_1_out, ~not_1_out, ~G2A_L, ~G2B_L);  // AND_Gate
  not not_5 (not_5_out, not_2_out);
  not not_6 (not_6_out, not_3_out);
  not not_7 (not_7_out, not_4_out);
  nand nand_1 (Y0_L, not_2_out, not_3_out, not_4_out, and_1_out);
  nand nand_2 (Y0_L_2, not_5_out, not_3_out, not_4_out, and_1_out);
  nand nand_3 (Y0_L_3, not_2_out, not_6_out, not_4_out, and_1_out);
  nand nand_4 (Y0_L_4, not_5_out, not_6_out, not_4_out, and_1_out);
  nand nand_5 (Y0_L_5, not_2_out, not_3_out, not_7_out, and_1_out);
  nand nand_6 (Y0_L_6, not_5_out, not_3_out, not_7_out, and_1_out);
  nand nand_7 (Y0_L_7, not_2_out, not_6_out, not_7_out, and_1_out);
  nand nand_8 (Y0_L_8, not_5_out, not_6_out, not_7_out, and_1_out);
endmodule

module \_4ä½_å__æ__éªŒç_µè  (
  input  in_1,
  input  in_2,
  input  in_3,
  input  in_4,
  output out_5
);

  wire xor_1_out, xor_2_out;

  xor xor_1 (xor_1_out, in_1, in_2);
  xor xor_2 (xor_2_out, in_3, in_4);
  xor xor_3 (out_5, xor_1_out, xor_2_out);
endmodule
