// Logisim project lab6.circ as structural Verilog
module \单周期CPU  (
  input  [31:0] Initial_Address,
  output halt
);

  wire alu_1_zero, ALUASrc, branch_1_nxtasrc, branch_1_nxtbsrc, clk, Halt0, MemToReg, MemWr, not_1_out,
       or_1_out, RegWr, RESET;
  wire [1:0] ALUBSrc;
  wire [2:0] Branch, ExtOp, funct3, MemOp;
  wire [3:0] ALUctr;
  wire [6:0] funct7, opcode;
  wire [15:0] alu_1_s_2, counter_1_q;
  wire [31:0] alu_1_s, idu_1_busa, idu_1_busb, idu_1_dataa, idu_1_datab, idu_1_imm, ifu_1_pc, IR,
       multiplexer_1_out, \数据储存器_1_dataout ;

  Clock clock_1 (.out(clk));
  Button u_Reset (.out(RESET));
  IFU ifu_1 (
    .CLK(clk), .Reset(RESET), .Halt(halt), .NxtASrc(branch_1_nxtasrc), .NxtBSrc(branch_1_nxtbsrc),
    .Initial_Address(Initial_Address), .Imm(idu_1_imm), .BusA(idu_1_busa), .PC(ifu_1_pc), .IR(IR));
  \控制器  \u_控制器_1  (
    .funct3(funct3), .opcode(opcode), .Branch(Branch), .MemOp(MemOp), .ALUASrc(ALUASrc), .ALUBSrc(ALUBSrc),
    .ALUctr(ALUctr), .MemtoReg(MemToReg), .RegWr(RegWr), .MemWr(MemWr), .ExtOp(ExtOp), .funct7(funct7),
    .halt(halt));
  IDU idu_1 (
    .ExtOp(ExtOp), .RegWr(RegWr), .OpCode(opcode), .ALUASrc(ALUASrc), .ALUBSrc(ALUBSrc), .Funct3(funct3),
    .CLK(clk), .Funct7(funct7), .IR(IR), .BusW(multiplexer_1_out), .PC(ifu_1_pc), .DataA(idu_1_dataa),
    .BusB(idu_1_busb), .DataB(idu_1_datab), .Imm(idu_1_imm), .BusA(idu_1_busa));
  or or_1 (or_1_out, Halt0, halt);
  Branch branch_1 (
    .Branch(Branch), .NxtASrc(branch_1_nxtasrc), .Zero(alu_1_zero), .NxtBSrc(branch_1_nxtbsrc),
    .Result0(alu_1_s[0]));
  ALU alu_1 (
    .A(idu_1_dataa), .B(idu_1_datab), .S({alu_1_s[31:18], alu_1_s_2, alu_1_s[1:0]}), .ALUctr(ALUctr),
    .Zero(alu_1_zero));
  Comparator #(.width(32)) comparator_1 (.a(IR), .b(32'h6f), .eq(Halt0));  // open: gt, lt
  // Probe on counter_1_q
  Counter #(.width(16), .max('hffff), .trigger("falling"), .behavior("old")) counter_1 (
    .count(not_1_out), .Q(counter_1_q), .clk(clk), .clr(RESET));  // open: load, D, carry, preset
  not not_1 (not_1_out, or_1_out);
  \数据储存器  \u_数据储存器_1  (
    .Addr(alu_1_s_2), .Din(idu_1_busb), .DataOut(\数据储存器_1_dataout ), .CLK(clk), .CLR(RESET), .MemOp(MemOp),
    .WE(MemWr), .SEL(1'b1));
  Multiplexer #(.width(32), .enable("false")) multiplexer_1 (
    .in0({alu_1_s[31:18], alu_1_s_2, alu_1_s[1:0]}), .in1(\数据储存器_1_dataout ), .out(multiplexer_1_out),
    .sel(MemToReg));

  // Other names for the same wires on the sheet: Init_Addr[31:0] = Initial_Address

  // Notes on the sheet:
  //   输入信号
  //   RV32I单周期CPU设计
  //   输出信号
endmodule

module \控制器  (
  input  [6:0] opcode,
  input  [2:0] funct3,
  input  [6:0] funct7,
  output [2:0] ExtOp,
  output RegWr,
  output ALUASrc,
  output [1:0] ALUBSrc,
  output [3:0] ALUctr,
  output [2:0] Branch,
  output MemtoReg,
  output [2:0] MemOp,
  output MemWr,
  output halt
);

  wire and_1_out, and_2_out, and_3_out, and_4_out, and_5_out, and_6_out, and_7_out, and_8_out, and_9_out,
       and_10_out, and_11_out, and_12_out, I_Arith, J_jal, J_jalr, or_1_out, or_5_out, or_8_out, or_9_out,
       or_10_out, R_Arith, U_auipc, U_lui;

  Comparator #(.width(7)) comparator_1 (.a(opcode), .b(7'b0110111), .eq(U_lui));  // open: gt, lt
  Comparator #(.width(7)) comparator_2 (.a(opcode), .b(7'b1100111), .eq(J_jalr));  // open: gt, lt
  Comparator #(.width(7)) comparator_3 (.a(opcode), .b(7'b0010111), .eq(U_auipc));  // open: gt, lt
  Comparator #(.width(7)) comparator_4 (.a(opcode), .b(7'b1100011), .eq(Branch[2]));  // open: gt, lt
  or or_1 (or_1_out, U_lui, U_auipc);
  or or_2 (ALUBSrc[0], J_jal, J_jalr);
  and and_1 (and_1_out, Branch[2], funct3[2]);
  and and_2 (and_2_out, Branch[2], funct3[0]);
  and and_3 (and_3_out, funct3[2], ~funct3[1], funct3[0]);  // AND_Gate
  and and_4 (and_4_out, funct3[2], I_Arith);
  and and_5 (and_5_out, R_Arith, funct3[2]);
  and and_6 (and_6_out, funct3[1], I_Arith);
  and and_7 (and_7_out, funct3[1], R_Arith);
  and and_8 (and_8_out, R_Arith, funct3[0]);
  and and_9 (and_9_out, I_Arith, funct3[0]);
  and and_10 (and_10_out, Branch[2], funct3[1]);
  or or_3 (ALUASrc, U_auipc, ALUBSrc[0]);
  or or_4 (ALUBSrc[1], or_1_out, I_Arith, MemtoReg, MemWr);
  or or_5 (or_5_out, MemtoReg, MemWr);
  or or_6 (Branch[1], and_1_out, J_jalr);
  or or_7 (Branch[0], J_jal, and_2_out);
  and and_11 (and_11_out, and_3_out, funct7[5], I_Arith);
  and and_12 (and_12_out, R_Arith, funct7[5]);
  or or_8 (or_8_out, and_4_out, and_5_out);
  or or_9 (or_9_out, and_6_out, and_7_out, Branch[2]);
  or or_10 (or_10_out, and_8_out, and_9_out, and_10_out);
  Comparator #(.width(7)) comparator_5 (.a(opcode), .b(7'b0010011), .eq(I_Arith));  // open: gt, lt
  Comparator #(.width(7)) comparator_6 (.a(opcode), .b(7'b0000011), .eq(MemtoReg));  // open: gt, lt
  or or_11 (RegWr, or_1_out, ALUBSrc[0], I_Arith, R_Arith, MemtoReg);
  MemOp memop_1 (
    ._2(funct3[2]), ._1(funct3[1]), ._0(funct3[0]), ._2_2(MemOp[2]), ._1_2(MemOp[1]), ._0_2(MemOp[0]),
    .s(or_5_out));
  or or_12 (ALUctr[3], and_11_out, U_lui, and_12_out);
  or or_13 (ALUctr[2], U_lui, or_8_out);
  or or_14 (ALUctr[1], U_lui, or_9_out);
  or or_15 (ALUctr[0], U_lui, or_10_out);
  Comparator #(.width(7)) comparator_7 (.a(opcode), .b(7'b0110011), .eq(R_Arith));  // open: gt, lt
  Comparator #(.width(7)) comparator_8 (.a(opcode), .b(7'b0100011), .eq(MemWr));  // open: gt, lt
  Comparator #(.width(7)) comparator_9 (.a(opcode), .b(7'b1101111), .eq(J_jal));  // open: gt, lt
  Comparator #(.width(7)) comparator_10 (.a(opcode), .b({7{1'b0}}), .eq(halt));  // open: gt, lt
  Extop extop_1 (
    .a(opcode[6]), .x(ExtOp[2]), .b(opcode[5]), .y(ExtOp[1]), .c(opcode[4]), .z(ExtOp[0]), .d(opcode[3]),
    .e(opcode[2]), .f(opcode[1]), .g(opcode[0]));

  // Other names for the same wires on the sheet: B_Instr = Branch[2]; I_load = MemtoReg; S_Instr = MemWr

  // Notes on the sheet:
  //   输入信号
  //   提示：根据指令种类和代码，把7位指令code用一位标志位来表示。
  //   输出信号
endmodule

module Extop (
  input  a,
  input  b,
  input  c,
  input  d,
  input  e,
  input  f,
  input  g,
  output x,
  output y,
  output z
);

  wire and_2_out, and_3_out, not_1_out, not_2_out, not_3_out, not_4_out;

  not not_1 (not_1_out, f);
  not not_2 (not_2_out, e);
  not not_3 (not_3_out, a);
  not not_4 (not_4_out, e);
  or or_1 (x, not_1_out, d);
  and and_1 (y, b, not_2_out);
  and and_2 (and_2_out, not_3_out, e);
  or or_2 (z, and_2_out, and_3_out);
  and and_3 (and_3_out, a, not_4_out);
endmodule

module MemOp (
  input  _2,
  input  _1,
  input  _0,
  input  s,
  output _2_2,
  output _1_2,
  output _0_2
);

  wire and_1_out, and_2_out, not_1_out, not_2_out, not_3_out, not_4_out;

  not not_1 (not_1_out, _2);
  not not_2 (not_2_out, _1);
  not not_3 (not_3_out, _1);
  not not_4 (not_4_out, _0);
  and and_1 (and_1_out, not_1_out, not_2_out);
  and and_2 (and_2_out, not_3_out, not_4_out);
  and and_3 (_2_2, and_1_out, s);
  and and_4 (_1_2, _0, s);
  and and_5 (_0_2, and_2_out, s);
endmodule

module ALU (
  input  [31:0] A,
  input  [31:0] B,
  input  [3:0] ALUctr,
  output [31:0] S,
  output Zero
);

  wire \alu操作控制信号生成部件_1_alctr , \alu操作控制信号生成部件_1_sftctr , \alu操作控制信号生成部件_1_sigctr , \alu操作控制信号生成部件_1_subctr ,
       multiplexer_2_out, \n32位加法器_1_cf , \n32位加法器_1_of , \n32位加法器_1_sf , xor_3_out;
  wire [2:0] \alu操作控制信号生成部件_1_opctr ;
  wire [31:0] and_1_out, bit_extender_1_out, bit_extender_2_out, \n32位加法器_1_s , \n32位桶形移位器_1_dataout ,
       or_1_out, xor_1_out, xor_2_out;

  assign bit_extender_1_out = {{31{\alu操作控制信号生成部件_1_subctr }}, \alu操作控制信号生成部件_1_subctr };  // Bit_Extender bit_extender_1
  assign and_1_out = A & B;  // AND_Gate and_1, 32 bits wide
  assign or_1_out = A | B;  // OR_Gate or_1, 32 bits wide
  assign xor_1_out = A ^ B;  // XOR_Gate xor_1, 32 bits wide
  \_32位桶形移位器  \u_32位桶形移位器_1  (
    .L_R(\alu操作控制信号生成部件_1_sftctr ), .shamt(B[4:0]), .DataIn(A), .DataOut(\n32位桶形移位器_1_dataout ),
    .A_L(\alu操作控制信号生成部件_1_alctr ));
  assign xor_2_out = B ^ bit_extender_1_out;  // XOR_Gate xor_2, 32 bits wide
  \_32位加法器  \u_32位加法器_1  (
    .Cin(\alu操作控制信号生成部件_1_subctr ), .X(A), .Y(xor_2_out), .S(\n32位加法器_1_s ), .OF(\n32位加法器_1_of ),
    .CF(\n32位加法器_1_cf ), .ZF(Zero), .SF(\n32位加法器_1_sf ));  // open: Cout
  xor xor_3 (xor_3_out, \n32位加法器_1_of , \n32位加法器_1_sf );
  Multiplexer #(.select(3), .width(32), .enable("false")) multiplexer_1 (
    .in0(\n32位加法器_1_s ), .in1(and_1_out), .in2(or_1_out), .in3(xor_1_out), .in4(\n32位桶形移位器_1_dataout ),
    .in5(B), .in6(bit_extender_2_out), .out(S), .sel(\alu操作控制信号生成部件_1_opctr ));  // open: in7
  \ALU操作控制信号生成部件  \alu操作控制信号生成部件_1  (
    .ALUctr(ALUctr), .SUBctr(\alu操作控制信号生成部件_1_subctr ), .SFTctr(\alu操作控制信号生成部件_1_sftctr ),
    .SIGctr(\alu操作控制信号生成部件_1_sigctr ), .ALctr(\alu操作控制信号生成部件_1_alctr ), .OPctr(\alu操作控制信号生成部件_1_opctr ));
  // Probe on A
  // Probe on B
  // Probe on S
  Multiplexer #(.enable("false")) multiplexer_2 (
    .in0(\n32位加法器_1_cf ), .in1(xor_3_out), .out(multiplexer_2_out), .sel(\alu操作控制信号生成部件_1_sigctr ));
  assign bit_extender_2_out = {{31{1'b0}}, multiplexer_2_out};  // Bit_Extender bit_extender_2

  // Other names for the same wires on the sheet: Result[31:0] = S

  // Notes on the sheet:
  //   ALUctr: pull=down
  //   B: pull=down
  //   A: pull=down
  //   输入引脚区
  //   32位算术逻辑运算单元ALU
  //   功能说明:32位ALU，输入32位操作数A、B，4位控制信号ALUctr，输出32位结果Reseult和1位Zero标志位
  //   输出引脚区
  //   操作数和结果
endmodule

module Regfiles (
  input  [4:0] R1_num,
  input  [31:0] Din,
  input  [4:0] R2_num,
  input  [4:0] Write_Reg_num,
  input  Write_Enable,
  input  Clock,
  output [31:0] Reg1Out,
  output [31:0] Reg2Out
);

  wire and_1_out, and_2_out, and_3_out, and_4_out, and_5_out, and_6_out, and_7_out, and_8_out, and_9_out,
       and_10_out, and_11_out, and_12_out, and_13_out, and_14_out, and_15_out, and_16_out, and_17_out,
       and_18_out, and_19_out, and_20_out, and_21_out, and_22_out, and_23_out, and_24_out, and_25_out,
       and_26_out, and_27_out, and_28_out, and_29_out, and_30_out, and_31_out, and_32_out, and_33_out,
       and_34_out, and_35_out, and_36_out, decoder_1_out0, decoder_1_out1, decoder_1_out2, decoder_1_out3,
       decoder_2_out0, decoder_2_out1, decoder_2_out2, decoder_2_out3, decoder_2_out4, decoder_2_out5,
       decoder_2_out6, decoder_2_out7, decoder_3_out0, decoder_3_out1, decoder_3_out2, decoder_3_out3,
       decoder_3_out4, decoder_3_out5, decoder_3_out6, decoder_3_out7, decoder_4_out0, decoder_4_out1,
       decoder_4_out2, decoder_4_out3, decoder_4_out4, decoder_4_out5, decoder_4_out6, decoder_4_out7,
       decoder_5_out0, decoder_5_out1, decoder_5_out2, decoder_5_out3, decoder_5_out4, decoder_5_out5,
       decoder_5_out7;
  wire [31:0] register_1_q, register_2_q, register_3_q, register_4_q, register_5_q, register_6_q,
       register_7_q, register_8_q, register_9_q, register_10_q, register_11_q, register_12_q, register_13_q,
       register_14_q, register_15_q, register_16_q, register_17_q, register_18_q, register_19_q,
       register_20_q, register_21_q, register_22_q, register_23_q, register_24_q, register_25_q,
       register_26_q, register_27_q, register_28_q, register_29_q, register_30_q, register_31_q,
       register_32_q;

  Decoder #(.select(2), .enable("false")) decoder_1 (
    .out0(decoder_1_out0), .out1(decoder_1_out1), .out2(decoder_1_out2), .out3(decoder_1_out3),
    .sel(Write_Reg_num[4:3]));
  Decoder #(.select(3), .enable("false")) decoder_2 (
    .out0(decoder_2_out0), .out1(decoder_2_out1), .out2(decoder_2_out2), .out3(decoder_2_out3),
    .out4(decoder_2_out4), .out5(decoder_2_out5), .out6(decoder_2_out6), .out7(decoder_2_out7),
    .sel(Write_Reg_num[2:0]));
  Decoder #(.select(3), .enable("false")) decoder_3 (
    .out0(decoder_3_out0), .out1(decoder_3_out1), .out2(decoder_3_out2), .out3(decoder_3_out3),
    .out4(decoder_3_out4), .out5(decoder_3_out5), .out6(decoder_3_out6), .out7(decoder_3_out7),
    .sel(Write_Reg_num[2:0]));
  Decoder #(.select(3), .enable("false")) decoder_4 (
    .out0(decoder_4_out0), .out1(decoder_4_out1), .out2(decoder_4_out2), .out3(decoder_4_out3),
    .out4(decoder_4_out4), .out5(decoder_4_out5), .out6(decoder_4_out6), .out7(decoder_4_out7),
    .sel(Write_Reg_num[2:0]));
  Decoder #(.select(3), .enable("false")) decoder_5 (
    .out0(decoder_5_out0), .out1(decoder_5_out1), .out2(decoder_5_out2), .out3(decoder_5_out3),
    .out4(decoder_5_out4), .out5(decoder_5_out5), .out6(decoder_5_out5), .out7(decoder_5_out7),
    .sel(Write_Reg_num[2:0]));
  and and_1 (and_1_out, Write_Enable, decoder_1_out0);
  and and_2 (and_2_out, decoder_1_out1, Write_Enable);
  and and_3 (and_3_out, decoder_1_out2, Write_Enable);
  and and_4 (and_4_out, decoder_1_out3, Write_Enable);
  and and_5 (and_5_out, decoder_2_out0, and_1_out);
  and and_6 (and_6_out, decoder_2_out1, and_1_out);
  and and_7 (and_7_out, decoder_2_out2, and_1_out);
  and and_8 (and_8_out, decoder_2_out3, and_1_out);
  and and_9 (and_9_out, decoder_2_out4, and_1_out);
  and and_10 (and_10_out, decoder_2_out5, and_1_out);
  and and_11 (and_11_out, decoder_2_out6, and_1_out);
  and and_12 (and_12_out, decoder_2_out7, and_1_out);
  and and_13 (and_13_out, decoder_3_out0, and_2_out);
  and and_14 (and_14_out, decoder_3_out1, and_2_out);
  and and_15 (and_15_out, decoder_3_out2, and_2_out);
  and and_16 (and_16_out, decoder_3_out3, and_2_out);
  and and_17 (and_17_out, decoder_3_out4, and_2_out);
  and and_18 (and_18_out, decoder_3_out5, and_2_out);
  and and_19 (and_19_out, decoder_3_out6, and_2_out);
  and and_20 (and_20_out, decoder_3_out7, and_2_out);
  and and_21 (and_21_out, decoder_4_out0, and_3_out);
  and and_22 (and_22_out, decoder_4_out1, and_3_out);
  and and_23 (and_23_out, decoder_4_out2, and_3_out);
  and and_24 (and_24_out, decoder_4_out3, and_3_out);
  and and_25 (and_25_out, decoder_4_out4, and_3_out);
  and and_26 (and_26_out, decoder_4_out5, and_3_out);
  and and_27 (and_27_out, decoder_4_out6, and_3_out);
  and and_28 (and_28_out, decoder_4_out7, and_3_out);
  and and_29 (and_29_out, decoder_5_out0, and_4_out);
  and and_30 (and_30_out, decoder_5_out1, and_4_out);
  and and_31 (and_31_out, decoder_5_out2, and_4_out);
  and and_32 (and_32_out, decoder_5_out3, and_4_out);
  and and_33 (and_33_out, decoder_5_out4, and_4_out);
  and and_34 (and_34_out, decoder_5_out5, and_4_out);
  and and_35 (and_35_out, decoder_5_out5, and_4_out);
  and and_36 (and_36_out, decoder_5_out7, and_4_out);
  Register #(.width(32), .trigger("falling"), .Select("low")) register_1 (
    .en(and_5_out), .Q(register_1_q), .clk(Clock));  // open: D, clr
  Register #(.width(32), .trigger("falling"), .Select("low")) register_2 (
    .D(Din), .en(and_6_out), .Q(register_2_q), .clk(Clock));  // open: clr
  Register #(.width(32), .trigger("falling"), .Select("low")) register_3 (
    .D(Din), .en(and_7_out), .Q(register_3_q), .clk(Clock));  // open: clr
  Register #(.width(32), .trigger("falling"), .Select("low")) register_4 (
    .D(Din), .en(and_8_out), .Q(register_4_q), .clk(Clock));  // open: clr
  Register #(.width(32), .trigger("falling"), .Select("low")) register_5 (
    .D(Din), .en(and_9_out), .Q(register_5_q), .clk(Clock));  // open: clr
  Register #(.width(32), .trigger("falling"), .Select("low")) register_6 (
    .D(Din), .en(and_10_out), .Q(register_6_q), .clk(Clock));  // open: clr
  Register #(.width(32), .trigger("falling"), .Select("low")) register_7 (
    .D(Din), .en(and_11_out), .Q(register_7_q), .clk(Clock));  // open: clr
  Register #(.width(32), .trigger("falling"), .Select("low")) register_8 (
    .D(Din), .en(and_12_out), .Q(register_8_q), .clk(Clock));  // open: clr
  Register #(.width(32), .trigger("falling"), .Select("low")) register_9 (
    .D(Din), .en(and_13_out), .Q(register_9_q), .clk(Clock));  // open: clr
  Register #(.width(32), .trigger("falling"), .Select("low")) register_10 (
    .D(Din), .en(and_14_out), .Q(register_10_q), .clk(Clock));  // open: clr
  Register #(.width(32), .trigger("falling"), .Select("low")) register_11 (
    .D(Din), .en(and_15_out), .Q(register_11_q), .clk(Clock));  // open: clr
  Register #(.width(32), .trigger("falling"), .Select("low")) register_12 (
    .D(Din), .en(and_16_out), .Q(register_12_q), .clk(Clock));  // open: clr
  Register #(.width(32), .trigger("falling"), .Select("low")) register_13 (
    .D(Din), .en(and_17_out), .Q(register_13_q), .clk(Clock));  // open: clr
  Register #(.width(32), .trigger("falling"), .Select("low")) register_14 (
    .D(Din), .en(and_18_out), .Q(register_14_q), .clk(Clock));  // open: clr
  Register #(.width(32), .trigger("falling"), .Select("low")) register_15 (
    .D(Din), .en(and_19_out), .Q(register_15_q), .clk(Clock));  // open: clr
  Register #(.width(32), .trigger("falling"), .Select("low")) register_16 (
    .D(Din), .en(and_20_out), .Q(register_16_q), .clk(Clock));  // open: clr
  Register #(.width(32), .trigger("falling"), .Select("low")) register_17 (
    .D(Din), .en(and_21_out), .Q(register_17_q), .clk(Clock));  // open: clr
  Register #(.width(32), .trigger("falling"), .Select("low")) register_18 (
    .D(Din), .en(and_22_out), .Q(register_18_q), .clk(Clock));  // open: clr
  Register #(.width(32), .trigger("falling"), .Select("low")) register_19 (
    .D(Din), .en(and_23_out), .Q(register_19_q), .clk(Clock));  // open: clr
  Register #(.width(32), .trigger("falling"), .Select("low")) register_20 (
    .D(Din), .en(and_24_out), .Q(register_20_q), .clk(Clock));  // open: clr
  Register #(.width(32), .trigger("falling"), .Select("low")) register_21 (
    .D(Din), .en(and_25_out), .Q(register_21_q), .clk(Clock));  // open: clr
  Register #(.width(32), .trigger("falling"), .Select("low")) register_22 (
    .D(Din), .en(and_26_out), .Q(register_22_q), .clk(Clock));  // open: clr
  Register #(.width(32), .trigger("falling"), .Select("low")) register_23 (
    .D(Din), .en(and_27_out), .Q(register_23_q), .clk(Clock));  // open: clr
  Register #(.width(32), .trigger("falling"), .Select("low")) register_24 (
    .D(Din), .en(and_28_out), .Q(register_24_q), .clk(Clock));  // open: clr
  Register #(.width(32), .trigger("falling"), .Select("low")) register_25 (
    .D(Din), .en(and_29_out), .Q(register_25_q), .clk(Clock));  // open: clr
  Register #(.width(32), .trigger("falling"), .Select("low")) register_26 (
    .D(Din), .en(and_30_out), .Q(register_26_q), .clk(Clock));  // open: clr
  Register #(.width(32), .trigger("falling"), .Select("low")) register_27 (
    .D(Din), .en(and_31_out), .Q(register_27_q), .clk(Clock));  // open: clr
  Register #(.width(32), .trigger("falling"), .Select("low")) register_28 (
    .D(Din), .en(and_32_out), .Q(register_28_q), .clk(Clock));  // open: clr
  Register #(.width(32), .trigger("falling"), .Select("low")) register_29 (
    .D(Din), .en(and_33_out), .Q(register_29_q), .clk(Clock));  // open: clr
  Register #(.width(32), .trigger("falling"), .Select("low")) register_30 (
    .D(Din), .en(and_34_out), .Q(register_30_q), .clk(Clock));  // open: clr
  Register #(.width(32), .trigger("falling"), .Select("low")) register_31 (
    .D(Din), .en(and_35_out), .Q(register_31_q), .clk(Clock));  // open: clr
  Register #(.width(32), .trigger("falling"), .Select("low")) register_32 (
    .D(Din), .en(and_36_out), .Q(register_32_q), .clk(Clock));  // open: clr
  Multiplexer #(.select(5), .width(32), .enable("false")) multiplexer_1 (
    .in0(register_1_q), .in1(register_2_q), .in2(register_3_q), .in3(register_4_q), .in4(register_5_q),
    .in5(register_6_q), .in6(register_7_q), .in7(register_8_q), .in8(register_9_q), .in9(register_10_q),
    .in10(register_11_q), .in11(register_12_q), .in12(register_13_q), .in13(register_14_q),
    .in14(register_15_q), .in15(register_16_q), .in16(register_17_q), .in17(register_18_q),
    .in18(register_19_q), .in19(register_20_q), .in20(register_21_q), .in21(register_22_q),
    .in22(register_23_q), .in23(register_24_q), .in24(register_25_q), .in25(register_26_q),
    .in26(register_27_q), .in27(register_28_q), .in28(register_29_q), .in29(register_30_q),
    .in30(register_31_q), .in31(register_32_q), .out(Reg1Out), .sel(R1_num));
  Multiplexer #(.select(5), .width(32), .enable("false")) multiplexer_2 (
    .in0(register_1_q), .in1(register_2_q), .in2(register_3_q), .in3(register_4_q), .in4(register_5_q),
    .in5(register_6_q), .in6(register_7_q), .in7(register_8_q), .in8(register_9_q), .in9(register_10_q),
    .in10(register_11_q), .in11(register_12_q), .in12(register_13_q), .in13(register_14_q),
    .in14(register_15_q), .in15(register_16_q), .in16(register_17_q), .in17(register_18_q),
    .in18(register_19_q), .in19(register_20_q), .in20(register_21_q), .in21(register_22_q),
    .in22(register_23_q), .in23(register_24_q), .in24(register_25_q), .in25(register_26_q),
    .in26(register_27_q), .in27(register_28_q), .in28(register_29_q), .in29(register_30_q),
    .in30(register_31_q), .in31(register_32_q), .out(Reg2Out), .sel(R2_num));

  // Other names for the same wires on the sheet: CLK = Clock; RA[4:0] = R1_num; RB[4:0] = R2_num; RDA[31:0] = Reg1Out;
  //   RDB[31:0] = Reg2Out; RW[4:0] = Write_Reg_num; WE = Write_Enable
endmodule

module IDU (
  input  [31:0] IR,
  input  [31:0] BusW,
  input  [31:0] PC,
  input  [2:0] ExtOp,
  input  RegWr,
  input  ALUASrc,
  input  [1:0] ALUBSrc,
  input  CLK,
  output [31:0] DataA,
  output [31:0] DataB,
  output [31:0] BusA,
  output [6:0] OpCode,
  output [31:0] BusB,
  output [31:0] Imm,
  output [2:0] Funct3,
  output [6:0] Funct7
);

  \立即数扩展器  \u_立即数扩展器_1  (.Instr(IR), .Extop(ExtOp), .imm(Imm));
  Regfiles regfiles_1 (
    .R1_num(IR[19:15]), .Din(BusW), .R2_num(IR[24:20]), .Write_Reg_num(IR[11:7]), .Write_Enable(RegWr),
    .Clock(CLK), .Reg1Out(BusA), .Reg2Out(BusB));
  Multiplexer #(.width(32), .enable("false")) multiplexer_1 (.in0(BusA), .in1(PC), .out(DataA), .sel(ALUASrc));
  Multiplexer #(.select(2), .width(32), .enable("false")) multiplexer_2 (
    .in0(BusB), .in1(32'h4), .in2(Imm), .out(DataB), .sel(ALUBSrc));  // open: in3

  assign Funct3 = IR[14:12];
  assign Funct7 = IR[31:25];
  assign OpCode = IR[6:0];

  // Other names for the same wires on the sheet: DataIn[31:0] = BusB; op[6:0] = IR[6:0]

  // Notes on the sheet:
  //   BusW: pull=down
  //   PC: pull=down
  //   ExtOp: pull=down
  //   ALUASrc: pull=down
  //   ALUBSrc: pull=down
  //   RegWr: pull=down
  //   指令解析
  //   funct7 rs2 rs1 funct3 rd opcode
  //   输入信号
  //   访问寄存器堆
  //   输出信号
  //   输出数据
endmodule

module IFU (
  input  [31:0] Initial_Address,
  input  [31:0] Imm,
  input  [31:0] BusA,
  input  CLK,
  input  Reset,
  input  Halt,
  input  NxtASrc,
  input  NxtBSrc,
  output [31:0] PC,
  output [31:0] IR
);

  wire [31:0] adder_1_out, multiplexer_1_out, multiplexer_2_out, multiplexer_3_out;

  Multiplexer #(.width(32), .enable("false")) multiplexer_1 (
    .in0(PC), .in1(BusA), .out(multiplexer_1_out), .sel(NxtASrc));
  Adder #(.width(32)) adder_1 (.a(multiplexer_1_out), .b(multiplexer_2_out), .out(adder_1_out));  // open: cin, cout
  Multiplexer #(.width(32), .enable("false")) multiplexer_2 (
    .in0(32'h4), .in1(Imm), .out(multiplexer_2_out), .sel(NxtBSrc));
  Multiplexer #(.width(32), .enable("false")) multiplexer_3 (
    .in0(adder_1_out), .in1(Initial_Address), .out(multiplexer_3_out), .sel(Reset));
  Register #(.width(32), .trigger("falling"), .Select("low")) u_PC (
    .D(multiplexer_3_out), .Q(PC), .clk(CLK), .cs(Halt));  // open: en, clr, preset
  ROM #(.addrWidth(16), .dataWidth(32), .Select("high")) \u_指令存储器  (.addr(PC[17:2]), .data(IR));

  // Other names for the same wires on the sheet: Init_Addr[31:0] = Initial_Address

  // Notes on the sheet:
  //   NxtASrc: pull=down
  //   Imm: pull=down
  //   Halt: pull=down
  //   BusA: pull=down
  //   NxtBSrc: pull=down
  //   指令存储器的数据位设置为32位，地址位设置为16位。存储器按照32位字长编址，地址位最低2位舍弃。
  //   输入信号
  //   输出信号
  //   contents of 指令存储器 (hex, n*v repeats v):
  //   2503 100593 50633 586b3 269713 72803 472883 108f663 1172023 1072223 b686b3 fec6e2e3 40b60633
  //   fcb61ce3 6f
endmodule

module \数据储存器  (
  input  [15:0] Addr,
  input  [31:0] Din,
  input  CLK,
  input  CLR,
  input  [2:0] MemOp,
  input  WE,
  input  SEL,
  output [31:0] DataOut
);

  wire and_1_out, and_2_out, and_3_out, and_4_out, not_1_out, not_2_out, not_3_out, not_4_out;
  wire [7:0] ram_1_data, ram_2_data, ram_3_data, ram_4_data;
  wire [31:0] bit_extender_1_out, bit_extender_2_out, bit_extender_3_out, bit_extender_4_out;

  and and_1 (and_1_out, WE, ~MemOp[2]);  // AND_Gate
  RAM #(.addrWidth(16), .bus("separate"), .Select("high"), .simpleMode("false")) ram_1 (
    .addr(Addr), .din(Din[31:24]), .data(ram_1_data), .str(and_1_out), .sel(SEL), .clk(not_1_out), .clr(CLR));  // open: ld
  not not_1 (not_1_out, CLK);
  and and_2 (and_2_out, WE, ~MemOp[2]);  // AND_Gate
  not not_2 (not_2_out, CLK);
  RAM #(.addrWidth(16), .bus("separate"), .Select("high"), .simpleMode("false")) ram_2 (
    .addr(Addr), .din(Din[23:16]), .data(ram_2_data), .str(and_2_out), .sel(SEL), .clk(not_2_out), .clr(CLR));  // open: ld
  not not_3 (not_3_out, CLK);
  and and_3 (and_3_out, WE, ~MemOp[0]);  // AND_Gate
  RAM #(.addrWidth(16), .bus("separate"), .Select("high"), .simpleMode("false")) ram_3 (
    .addr(Addr), .din(Din[15:8]), .data(ram_3_data), .str(and_3_out), .sel(SEL), .clk(not_3_out), .clr(CLR));  // open: ld
  not not_4 (not_4_out, CLK);
  and and_4 (and_4_out, WE, 1'b1);
  RAM #(.addrWidth(16), .bus("separate"), .Select("high"), .simpleMode("false")) ram_4 (
    .addr(Addr), .din(Din[7:0]), .data(ram_4_data), .str(and_4_out), .sel(SEL), .clk(not_4_out), .clr(CLR));  // open: ld
  assign bit_extender_1_out = {{24{ram_4_data[7]}}, ram_4_data};  // Bit_Extender bit_extender_1
  assign bit_extender_2_out = {{24{1'b0}}, ram_4_data};  // Bit_Extender bit_extender_2
  assign bit_extender_3_out = {{16{1'b0}}, {ram_3_data, ram_4_data}};  // Bit_Extender bit_extender_3
  assign bit_extender_4_out = {{16{ram_3_data[7]}}, {ram_3_data, ram_4_data}};  // Bit_Extender bit_extender_4
  Multiplexer #(.select(3), .width(32), .enable("false")) multiplexer_1 (
    .in0({ram_1_data, ram_2_data, ram_3_data, ram_4_data}), .in1(bit_extender_2_out),
    .in2(bit_extender_3_out), .in5(bit_extender_1_out), .in6(bit_extender_4_out), .out(DataOut), .sel(MemOp));  // open: in3, in4, in7

  // Other names for the same wires on the sheet: Dout[31:0] = DataOut

  // Notes on the sheet:
  //   输入引脚区
  //   32位数据存储器，按字节分4片存储，可按照字节、半字和字进行存储；读取字节或半字时，支持0扩展和符号位扩展。
  //   为了后续实验中的引用，不要修改MemOp的编码定义，以及引脚名称和在布局图中位置。
  //   输出引脚区
endmodule

module Branch (
  input  [2:0] Branch,
  input  Zero,
  input  Result0,
  output NxtASrc,
  output NxtBSrc
);

  wire not_1_out, or_1_out;

  or or_1 (or_1_out, ~Result0, Zero);  // OR_Gate
  not not_1 (not_1_out, Zero);
  Multiplexer #(.select(3), .enable("false")) multiplexer_1 (
    .in0(1'b0), .in1(1'b1), .in2(1'b1), .in4(Zero), .in5(not_1_out), .in6(Result0), .in7(or_1_out),
    .out(NxtBSrc), .sel(Branch));  // open: in3
  Multiplexer #(.select(3), .enable("false")) multiplexer_2 (
    .in0(1'b0), .in1(1'b0), .in2(1'b1), .in4(1'b0), .in5(1'b0), .in6(1'b0), .in7(1'b0), .out(NxtASrc),
    .sel(Branch));  // open: in3

  // Notes on the sheet:
  //   Branch: pull=down
  //   Zero: pull=down
  //   输入信号
  //   输出信号
endmodule
